// Logisim project ALU.circ as structural Verilog: 2 circuits, main circuit main
// ALU
module main (
  input  RESET,
  input  Clock,
  input  L_Enabler,
  input  R_Enabler,
  input  Answer_Enabler,
  input  Status_Enabler,
  input  L7,
  input  L6,
  input  L5,
  input  L4,
  input  L3,
  input  L2,
  input  L1,
  input  L0,
  input  R7,
  input  R6,
  input  R5,
  input  R4,
  input  R3,
  input  R2,
  input  R1,
  input  R0,
  input  C2,
  input  C1,
  input  C0,
  output Status,
  output A7,
  output A6,
  output A5,
  output A4,
  output A3,
  output A2,
  output A1,
  output A0
);

  wire and_1_out, and_2_out, and_3_out, and_4_out, and_5_out, and_6_out, and_7_out, and_8_out, and_9_out,
       and_10_out, and_11_out, and_12_out, and_13_out, and_14_out, and_15_out, and_16_out, and_17_out,
       and_18_out, and_19_out, and_20_out, and_21_out, and_22_out, and_23_out, and_24_out, and_25_out,
       and_26_out, and_27_out, and_28_out, and_29_out, and_30_out, and_31_out, and_32_out, and_33_out,
       and_34_out, and_35_out, and_36_out, and_37_out, and_38_out, and_39_out, and_40_out, and_41_out,
       and_42_out, and_43_out, and_44_out, and_45_out, and_46_out, and_47_out, and_48_out, and_49_out,
       and_50_out, and_51_out, and_52_out, and_53_out, and_54_out, and_55_out, and_56_out, and_57_out,
       and_58_out, and_59_out, and_60_out, and_61_out, and_62_out, and_63_out, and_64_out, multiplier_1_s,
       multiplier_2_c_o, multiplier_2_s, multiplier_3_s, multiplier_4_c_o, multiplier_4_s, multiplier_5_c_o,
       multiplier_5_s, multiplier_6_s, multiplier_7_c_o, multiplier_7_s, multiplier_8_c_o, multiplier_8_s,
       multiplier_9_c_o, multiplier_9_s, multiplier_10_s, multiplier_11_c_o, multiplier_11_s,
       multiplier_12_c_o, multiplier_12_s, multiplier_13_c_o, multiplier_13_s, multiplier_14_c_o,
       multiplier_14_s, multiplier_15_s, multiplier_16_c_o, multiplier_16_s, multiplier_17_c_o,
       multiplier_17_s, multiplier_18_c_o, multiplier_18_s, multiplier_19_c_o, multiplier_19_s,
       multiplier_20_c_o, multiplier_20_s, multiplier_21_s, multiplier_22_c_o, multiplier_22_s,
       multiplier_23_c_o, multiplier_23_s, multiplier_24_c_o, multiplier_24_s, multiplier_25_c_o,
       multiplier_25_s, multiplier_26_c_o, multiplier_26_s, multiplier_27_c_o, multiplier_27_s,
       multiplier_28_s, multiplier_29_c_o, multiplier_29_s, multiplier_30_c_o, multiplier_30_s,
       multiplier_31_c_o, multiplier_31_s, multiplier_32_c_o, multiplier_32_s, multiplier_33_c_o,
       multiplier_33_s, multiplier_34_c_o, multiplier_34_s, multiplier_35_c_o, multiplier_35_s,
       multiplier_36_s, multiplier_37_c_o, multiplier_37_s, multiplier_38_c_o, multiplier_38_s,
       multiplier_39_c_o, multiplier_39_s, multiplier_40_c_o, multiplier_40_s, multiplier_41_c_o,
       multiplier_41_s, multiplier_42_c_o, multiplier_42_s, multiplier_43_c_o, multiplier_43_s,
       multiplier_44_c_o, multiplier_44_s, multiplier_45_c_o, multiplier_45_s, multiplier_46_c_o,
       multiplier_46_s, multiplier_47_c_o, multiplier_47_s, multiplier_48_c_o, multiplier_48_s,
       multiplier_49_c_o, multiplier_49_s, multiplier_50_c_o, multiplier_50_s, multiplier_51_c_o,
       multiplier_51_s, multiplier_52_c_o, multiplier_52_s, multiplier_53_c_o, multiplier_53_s,
       multiplier_54_c_o, multiplier_54_s, multiplier_55_c_o, multiplier_55_s, multiplier_56_c_o,
       multiplier_56_s, multiplier_57_c_o, multiplier_57_s, multiplier_58_c_o, multiplier_58_s,
       multiplier_59_c_o, multiplier_59_s, multiplier_60_c_o, multiplier_60_s, multiplier_61_c_o,
       multiplier_61_s, multiplier_62_c_o, multiplier_62_s, multiplier_63_c_o, multiplier_63_s,
       multiplier_64_c_o, multiplier_64_s, not_1_out, not_2_out, not_3_out, not_4_out, not_5_out, not_6_out,
       not_7_out, not_8_out, not_9_out, not_10_out, not_11_out, not_12_out, not_13_out, not_14_out,
       not_15_out, not_16_out, not_17_out, not_18_out, not_19_out, not_20_out, not_21_out, not_22_out,
       not_23_out, not_24_out, or_1_out, or_2_out, or_3_out, or_4_out, or_5_out, or_6_out, or_7_out,
       or_8_out, or_9_out, or_10_out, or_11_out, or_12_out, or_13_out, or_14_out, or_15_out, or_16_out,
       or_17_out, or_18_out, or_19_out, or_20_out, or_21_out, or_22_out, or_23_out, or_24_out, or_25_out,
       or_26_out, or_27_out, or_28_out, or_29_out, or_30_out, rising_8_bit_register_1_output_pin_0,
       rising_8_bit_register_1_output_pin_1, rising_8_bit_register_1_output_pin_2,
       rising_8_bit_register_1_output_pin_3, rising_8_bit_register_1_output_pin_4,
       rising_8_bit_register_1_output_pin_5, rising_8_bit_register_1_output_pin_6,
       rising_8_bit_register_1_output_pin_7, rising_8_bit_register_3_output_pin_0,
       rising_8_bit_register_3_output_pin_1, rising_8_bit_register_3_output_pin_2,
       rising_8_bit_register_3_output_pin_3, rising_8_bit_register_3_output_pin_4,
       rising_8_bit_register_3_output_pin_5, rising_8_bit_register_3_output_pin_6,
       rising_8_bit_register_3_output_pin_7, xor_1_out, xor_2_out, xor_3_out, xor_4_out, xor_5_out,
       xor_6_out, xor_7_out, xor_8_out, xor_9_out, xor_10_out, xor_11_out, xor_12_out, xor_13_out,
       xor_14_out, xor_15_out, xor_16_out, xor_17_out, xor_18_out, xor_19_out, xor_20_out, xor_21_out,
       xor_22_out, xor_23_out;

  not not_1 (not_1_out, C2);
  not not_2 (not_2_out, C0);
  and and_1 (and_1_out, not_2_out, not_4_out);
  or or_1 (or_1_out, and_1_out, and_2_out);
  not not_3 (not_3_out, C0);
  and and_2 (and_2_out, C0, C1);
  and and_3 (and_3_out, not_3_out, C1);
  not not_4 (not_4_out, C1);
  and and_4 (and_4_out, and_2_out, xor_5_out);
  and and_5 (and_5_out, and_1_out, or_4_out);
  and and_6 (and_6_out, C2, or_30_out);
  or or_2 (or_2_out, and_5_out, and_14_out, and_13_out, and_4_out, and_6_out);
  Rising_8_Bit_Register rising_8_bit_register_1 (
    .Enabler(L_Enabler), .Clock(Clock), .Input_Pin_0(L0), .Input_Pin_1(L1), .Input_Pin_2(L2),
    .Input_Pin_3(L3), .Input_Pin_4(L4), .Input_Pin_5(L5), .Input_Pin_6(L6), .Input_Pin_7(L7),
    .Output_Pin_0(rising_8_bit_register_1_output_pin_0), .Output_Pin_1(rising_8_bit_register_1_output_pin_1),
    .Output_Pin_2(rising_8_bit_register_1_output_pin_2), .Output_Pin_3(rising_8_bit_register_1_output_pin_3),
    .Output_Pin_4(rising_8_bit_register_1_output_pin_4), .Output_Pin_5(rising_8_bit_register_1_output_pin_5),
    .Output_Pin_6(rising_8_bit_register_1_output_pin_6), .Output_Pin_7(rising_8_bit_register_1_output_pin_7),
    .RESET(RESET));
  not not_5 (not_5_out, C1);
  and and_7 (and_7_out, C0, not_5_out);
  and and_8 (and_8_out, and_15_out, not_10_out);
  xor xor_1 (xor_1_out, not_8_out, and_8_out);
  not not_6 (not_6_out, or_7_out);
  and and_9 (and_9_out, xor_1_out, or_7_out);
  and and_10 (and_10_out, not_6_out, rising_8_bit_register_1_output_pin_7);
  or or_3 (or_3_out, and_9_out, and_10_out);
  and and_11 (and_11_out, or_3_out, rising_8_bit_register_3_output_pin_7);
  or or_4 (or_4_out, and_11_out, and_12_out);
  and and_12 (and_12_out, or_10_out, xor_3_out);
  or or_5 (or_5_out, xor_5_out, xor_8_out, xor_12_out, xor_16_out, xor_18_out);
  or or_6 (or_6_out, or_5_out, xor_20_out, xor_22_out, xor_23_out);
  not not_7 (not_7_out, or_6_out);
  and and_13 (and_13_out, not_7_out, and_7_out);
  and and_14 (and_14_out, and_3_out, or_6_out);
  not not_8 (not_8_out, rising_8_bit_register_1_output_pin_7);
  or or_7 (or_7_out, C1, C0);
  and and_15 (and_15_out, not_11_out, and_18_out);
  xor xor_2 (xor_2_out, not_10_out, and_15_out);
  not not_9 (not_9_out, or_7_out);
  and and_16 (and_16_out, xor_2_out, or_7_out);
  and and_17 (and_17_out, not_9_out, rising_8_bit_register_1_output_pin_6);
  or or_8 (or_8_out, and_16_out, and_17_out);
  xor xor_3 (xor_3_out, or_3_out, rising_8_bit_register_3_output_pin_7);
  not not_10 (not_10_out, rising_8_bit_register_1_output_pin_6);
  not not_11 (not_11_out, rising_8_bit_register_1_output_pin_5);
  and and_18 (and_18_out, not_12_out, and_26_out);
  xor xor_4 (xor_4_out, not_11_out, and_18_out);
  and and_19 (and_19_out, xor_4_out, or_7_out);
  or or_9 (or_9_out, and_19_out, and_23_out);
  or or_10 (or_10_out, and_24_out, and_25_out);
  xor xor_5 (xor_5_out, xor_3_out, or_10_out);
  and and_20 (and_20_out, not_1_out, or_1_out, xor_5_out);
  and and_21 (and_21_out, multiplier_36_s, C2);
  or or_11 (or_11_out, and_20_out, and_21_out);
  not not_12 (not_12_out, rising_8_bit_register_1_output_pin_4);
  not not_13 (not_13_out, rising_8_bit_register_1_output_pin_3);
  xor xor_6 (xor_6_out, not_12_out, and_26_out);
  not not_14 (not_14_out, or_7_out);
  and and_22 (and_22_out, xor_6_out, or_7_out);
  and and_23 (and_23_out, rising_8_bit_register_1_output_pin_5, not_14_out);
  and and_24 (and_24_out, or_8_out, rising_8_bit_register_3_output_pin_6);
  and and_25 (and_25_out, or_13_out, xor_7_out);
  not not_15 (not_15_out, rising_8_bit_register_1_output_pin_2);
  not not_16 (not_16_out, rising_8_bit_register_1_output_pin_1);
  and and_26 (and_26_out, and_29_out, not_13_out);
  not not_17 (not_17_out, or_7_out);
  and and_27 (and_27_out, rising_8_bit_register_1_output_pin_4, not_17_out);
  or or_12 (or_12_out, and_22_out, and_27_out);
  or or_13 (or_13_out, and_32_out, and_33_out);
  xor xor_7 (xor_7_out, or_8_out, rising_8_bit_register_3_output_pin_6);
  xor xor_8 (xor_8_out, xor_7_out, or_13_out);
  and and_28 (and_28_out, or_1_out, xor_8_out, not_1_out);
  D_Flip_Flop d_ff_1 (.clk(Clock), .D(or_2_out), .Q(Status), .en(Status_Enabler), .reset(RESET));  // open: Qn, preset
  not not_18 (not_18_out, rising_8_bit_register_1_output_pin_0);
  and and_29 (and_29_out, not_15_out, and_35_out);
  xor xor_9 (xor_9_out, not_13_out, and_29_out);
  not not_19 (not_19_out, or_7_out);
  and and_30 (and_30_out, xor_9_out, or_7_out);
  and and_31 (and_31_out, rising_8_bit_register_1_output_pin_3, not_19_out);
  or or_14 (or_14_out, and_30_out, and_31_out);
  and and_32 (and_32_out, or_9_out, rising_8_bit_register_3_output_pin_5);
  and and_33 (and_33_out, or_18_out, xor_11_out);
  and and_34 (and_34_out, multiplier_43_s, C2);
  or or_15 (or_15_out, and_28_out, and_34_out);
  and and_35 (and_35_out, and_39_out, not_16_out);
  xor xor_10 (xor_10_out, not_15_out, and_35_out);
  and and_36 (and_36_out, xor_10_out, or_7_out);
  and and_37 (and_37_out, rising_8_bit_register_1_output_pin_2, not_20_out);
  or or_16 (or_16_out, and_36_out, and_37_out);
  xor xor_11 (xor_11_out, or_9_out, rising_8_bit_register_3_output_pin_5);
  xor xor_12 (xor_12_out, xor_11_out, or_18_out);
  and and_38 (and_38_out, or_1_out, xor_12_out, not_1_out);
  and and_39 (and_39_out, not_18_out, or_20_out);
  xor xor_13 (xor_13_out, not_16_out, and_39_out);
  not not_20 (not_20_out, or_7_out);
  and and_40 (and_40_out, xor_13_out, or_7_out);
  or or_17 (or_17_out, and_40_out, and_44_out);
  and and_41 (and_41_out, or_12_out, rising_8_bit_register_3_output_pin_4);
  or or_18 (or_18_out, and_41_out, and_45_out);
  and and_42 (and_42_out, multiplier_49_s, C2);
  or or_19 (or_19_out, and_38_out, and_38_out, and_38_out, and_42_out);
  xor xor_14 (xor_14_out, not_18_out, or_20_out);
  not not_21 (not_21_out, or_7_out);
  and and_43 (and_43_out, xor_14_out, or_7_out);
  and and_44 (and_44_out, rising_8_bit_register_1_output_pin_1, not_21_out);
  and and_45 (and_45_out, or_22_out, xor_15_out);
  Rising_8_Bit_Register rising_8_bit_register_2 (
    .Enabler(Answer_Enabler), .Clock(Clock), .Input_Pin_0(or_29_out), .Input_Pin_1(or_28_out),
    .Input_Pin_2(or_27_out), .Input_Pin_3(or_25_out), .Input_Pin_4(or_23_out), .Input_Pin_5(or_19_out),
    .Input_Pin_6(or_15_out), .Input_Pin_7(or_11_out), .Output_Pin_0(A0), .Output_Pin_1(A1),
    .Output_Pin_2(A2), .Output_Pin_3(A3), .Output_Pin_4(A4), .Output_Pin_5(A5), .Output_Pin_6(A6),
    .Output_Pin_7(A7), .RESET(RESET));
  Rising_8_Bit_Register rising_8_bit_register_3 (
    .Enabler(R_Enabler), .Clock(Clock), .Input_Pin_0(R0), .Input_Pin_1(R1), .Input_Pin_2(R2),
    .Input_Pin_3(R3), .Input_Pin_4(R4), .Input_Pin_5(R5), .Input_Pin_6(R6), .Input_Pin_7(R7),
    .Output_Pin_0(rising_8_bit_register_3_output_pin_0), .Output_Pin_1(rising_8_bit_register_3_output_pin_1),
    .Output_Pin_2(rising_8_bit_register_3_output_pin_2), .Output_Pin_3(rising_8_bit_register_3_output_pin_3),
    .Output_Pin_4(rising_8_bit_register_3_output_pin_4), .Output_Pin_5(rising_8_bit_register_3_output_pin_5),
    .Output_Pin_6(rising_8_bit_register_3_output_pin_6), .Output_Pin_7(rising_8_bit_register_3_output_pin_7),
    .RESET(RESET));
  not not_22 (not_22_out, not_18_out);
  or or_20 (or_20_out, not_22_out, not_18_out);
  not not_23 (not_23_out, or_7_out);
  and and_46 (and_46_out, rising_8_bit_register_1_output_pin_0, not_23_out);
  or or_21 (or_21_out, and_43_out, and_46_out);
  or or_22 (or_22_out, and_48_out, and_49_out);
  xor xor_15 (xor_15_out, or_12_out, rising_8_bit_register_3_output_pin_4);
  xor xor_16 (xor_16_out, xor_15_out, or_22_out);
  and and_47 (and_47_out, or_1_out, xor_16_out, not_1_out);
  and and_48 (and_48_out, or_14_out, rising_8_bit_register_3_output_pin_3);
  and and_49 (and_49_out, or_24_out, xor_17_out);
  and and_50 (and_50_out, multiplier_54_s, C2);
  or or_23 (or_23_out, and_47_out, and_50_out);
  or or_24 (or_24_out, and_52_out, and_53_out);
  xor xor_17 (xor_17_out, or_14_out, rising_8_bit_register_3_output_pin_3);
  xor xor_18 (xor_18_out, xor_17_out, or_24_out);
  and and_51 (and_51_out, or_1_out, xor_18_out, not_1_out);
  and and_52 (and_52_out, or_16_out, rising_8_bit_register_3_output_pin_2);
  and and_53 (and_53_out, or_26_out, xor_19_out);
  and and_54 (and_54_out, multiplier_58_s, C2);
  or or_25 (or_25_out, and_51_out, and_51_out, and_54_out);
  xor xor_19 (xor_19_out, or_16_out, rising_8_bit_register_3_output_pin_2);
  and and_55 (and_55_out, rising_8_bit_register_3_output_pin_1, or_17_out);
  or or_26 (or_26_out, and_55_out, and_58_out);
  xor xor_20 (xor_20_out, xor_19_out, or_26_out);
  and and_56 (and_56_out, or_1_out, xor_20_out, not_1_out);
  and and_57 (and_57_out, multiplier_61_s, C2);
  or or_27 (or_27_out, and_56_out, and_56_out, and_57_out);
  and and_58 (and_58_out, and_59_out, xor_21_out);
  and and_59 (and_59_out, or_21_out, rising_8_bit_register_3_output_pin_0);
  xor xor_21 (xor_21_out, or_17_out, rising_8_bit_register_3_output_pin_1);
  xor xor_22 (xor_22_out, xor_21_out, and_59_out);
  and and_60 (and_60_out, or_1_out, xor_22_out, not_1_out);
  not not_24 (not_24_out, rising_8_bit_register_3_output_pin_0);
  xor xor_23 (xor_23_out, or_21_out, rising_8_bit_register_3_output_pin_0);
  and and_61 (and_61_out, or_1_out, xor_23_out, not_1_out);
  and and_62 (and_62_out, multiplier_63_s, C2);
  or or_28 (or_28_out, and_60_out, and_60_out, and_62_out);
  and and_63 (and_63_out, not_24_out, rising_8_bit_register_3_output_pin_0, rising_8_bit_register_3_output_pin_0);
  and and_64 (and_64_out, multiplier_64_s, C2);
  or or_29 (or_29_out, and_61_out, and_61_out, and_64_out);
  Multiplier multiplier_1 (
    .A(rising_8_bit_register_1_output_pin_7), .B(rising_8_bit_register_3_output_pin_7), .S_i(and_63_out),
    .C_i(multiplier_2_c_o), .S(multiplier_1_s));  // open: C_o
  Multiplier multiplier_2 (
    .A(rising_8_bit_register_1_output_pin_6), .B(rising_8_bit_register_3_output_pin_7), .S_i(and_63_out),
    .C_i(multiplier_4_c_o), .C_o(multiplier_2_c_o), .S(multiplier_2_s));
  Multiplier multiplier_3 (
    .A(rising_8_bit_register_1_output_pin_7), .B(rising_8_bit_register_3_output_pin_6), .S_i(multiplier_2_s),
    .C_i(multiplier_5_c_o), .S(multiplier_3_s));  // open: C_o
  Multiplier multiplier_4 (
    .A(rising_8_bit_register_1_output_pin_5), .B(rising_8_bit_register_3_output_pin_7), .S_i(and_63_out),
    .C_i(multiplier_7_c_o), .C_o(multiplier_4_c_o), .S(multiplier_4_s));
  Multiplier multiplier_5 (
    .A(rising_8_bit_register_1_output_pin_6), .B(rising_8_bit_register_3_output_pin_6), .S_i(multiplier_4_s),
    .C_i(multiplier_8_c_o), .C_o(multiplier_5_c_o), .S(multiplier_5_s));
  Multiplier multiplier_6 (
    .A(rising_8_bit_register_1_output_pin_7), .B(rising_8_bit_register_3_output_pin_5), .S_i(multiplier_5_s),
    .C_i(multiplier_9_c_o), .S(multiplier_6_s));  // open: C_o
  Multiplier multiplier_7 (
    .A(rising_8_bit_register_1_output_pin_4), .B(rising_8_bit_register_3_output_pin_7), .S_i(and_63_out),
    .C_i(multiplier_11_c_o), .C_o(multiplier_7_c_o), .S(multiplier_7_s));
  Multiplier multiplier_8 (
    .A(rising_8_bit_register_1_output_pin_5), .B(rising_8_bit_register_3_output_pin_6), .S_i(multiplier_7_s),
    .C_i(multiplier_12_c_o), .C_o(multiplier_8_c_o), .S(multiplier_8_s));
  Multiplier multiplier_9 (
    .A(rising_8_bit_register_1_output_pin_6), .B(rising_8_bit_register_3_output_pin_5), .S_i(multiplier_8_s),
    .C_i(multiplier_13_c_o), .C_o(multiplier_9_c_o), .S(multiplier_9_s));
  Multiplier multiplier_10 (
    .A(rising_8_bit_register_1_output_pin_7), .B(rising_8_bit_register_3_output_pin_4), .S_i(multiplier_9_s),
    .C_i(multiplier_14_c_o), .S(multiplier_10_s));  // open: C_o
  or or_30 (or_30_out, multiplier_1_s, multiplier_3_s, multiplier_6_s, multiplier_10_s, multiplier_15_s, multiplier_21_s, multiplier_28_s);
  Multiplier multiplier_11 (
    .A(rising_8_bit_register_1_output_pin_3), .B(rising_8_bit_register_3_output_pin_7), .S_i(and_63_out),
    .C_i(multiplier_16_c_o), .C_o(multiplier_11_c_o), .S(multiplier_11_s));
  Multiplier multiplier_12 (
    .A(rising_8_bit_register_1_output_pin_4), .B(rising_8_bit_register_3_output_pin_6),
    .S_i(multiplier_11_s), .C_i(multiplier_17_c_o), .C_o(multiplier_12_c_o), .S(multiplier_12_s));
  Multiplier multiplier_13 (
    .A(rising_8_bit_register_1_output_pin_5), .B(rising_8_bit_register_3_output_pin_5),
    .S_i(multiplier_12_s), .C_i(multiplier_18_c_o), .C_o(multiplier_13_c_o), .S(multiplier_13_s));
  Multiplier multiplier_14 (
    .A(rising_8_bit_register_1_output_pin_6), .B(rising_8_bit_register_3_output_pin_4),
    .S_i(multiplier_13_s), .C_i(multiplier_19_c_o), .C_o(multiplier_14_c_o), .S(multiplier_14_s));
  Multiplier multiplier_15 (
    .A(rising_8_bit_register_1_output_pin_7), .B(rising_8_bit_register_3_output_pin_3),
    .S_i(multiplier_14_s), .C_i(multiplier_20_c_o), .S(multiplier_15_s));  // open: C_o
  Multiplier multiplier_16 (
    .A(rising_8_bit_register_1_output_pin_2), .B(rising_8_bit_register_3_output_pin_7), .S_i(and_63_out),
    .C_i(multiplier_22_c_o), .C_o(multiplier_16_c_o), .S(multiplier_16_s));
  Multiplier multiplier_17 (
    .A(rising_8_bit_register_1_output_pin_3), .B(rising_8_bit_register_3_output_pin_6),
    .S_i(multiplier_16_s), .C_i(multiplier_23_c_o), .C_o(multiplier_17_c_o), .S(multiplier_17_s));
  Multiplier multiplier_18 (
    .A(rising_8_bit_register_1_output_pin_4), .B(rising_8_bit_register_3_output_pin_5),
    .S_i(multiplier_17_s), .C_i(multiplier_24_c_o), .C_o(multiplier_18_c_o), .S(multiplier_18_s));
  Multiplier multiplier_19 (
    .A(rising_8_bit_register_1_output_pin_5), .B(rising_8_bit_register_3_output_pin_4),
    .S_i(multiplier_18_s), .C_i(multiplier_25_c_o), .C_o(multiplier_19_c_o), .S(multiplier_19_s));
  Multiplier multiplier_20 (
    .A(rising_8_bit_register_1_output_pin_6), .B(rising_8_bit_register_3_output_pin_3),
    .S_i(multiplier_19_s), .C_i(multiplier_26_c_o), .C_o(multiplier_20_c_o), .S(multiplier_20_s));
  Multiplier multiplier_21 (
    .A(rising_8_bit_register_1_output_pin_7), .B(rising_8_bit_register_3_output_pin_2),
    .S_i(multiplier_20_s), .C_i(multiplier_27_c_o), .S(multiplier_21_s));  // open: C_o
  Multiplier multiplier_22 (
    .A(rising_8_bit_register_1_output_pin_1), .B(rising_8_bit_register_3_output_pin_7), .S_i(and_63_out),
    .C_i(multiplier_29_c_o), .C_o(multiplier_22_c_o), .S(multiplier_22_s));
  Multiplier multiplier_23 (
    .A(rising_8_bit_register_1_output_pin_2), .B(rising_8_bit_register_3_output_pin_6),
    .S_i(multiplier_22_s), .C_i(multiplier_30_c_o), .C_o(multiplier_23_c_o), .S(multiplier_23_s));
  Multiplier multiplier_24 (
    .A(rising_8_bit_register_1_output_pin_3), .B(rising_8_bit_register_3_output_pin_5),
    .S_i(multiplier_23_s), .C_i(multiplier_31_c_o), .C_o(multiplier_24_c_o), .S(multiplier_24_s));
  Multiplier multiplier_25 (
    .A(rising_8_bit_register_1_output_pin_4), .B(rising_8_bit_register_3_output_pin_4),
    .S_i(multiplier_24_s), .C_i(multiplier_32_c_o), .C_o(multiplier_25_c_o), .S(multiplier_25_s));
  Multiplier multiplier_26 (
    .A(rising_8_bit_register_1_output_pin_5), .B(rising_8_bit_register_3_output_pin_3),
    .S_i(multiplier_25_s), .C_i(multiplier_33_c_o), .C_o(multiplier_26_c_o), .S(multiplier_26_s));
  Multiplier multiplier_27 (
    .A(rising_8_bit_register_1_output_pin_6), .B(rising_8_bit_register_3_output_pin_2),
    .S_i(multiplier_26_s), .C_i(multiplier_34_c_o), .C_o(multiplier_27_c_o), .S(multiplier_27_s));
  Multiplier multiplier_28 (
    .A(rising_8_bit_register_1_output_pin_7), .B(rising_8_bit_register_3_output_pin_1),
    .S_i(multiplier_27_s), .C_i(multiplier_35_c_o), .S(multiplier_28_s));  // open: C_o
  Multiplier multiplier_29 (
    .A(rising_8_bit_register_1_output_pin_0), .B(rising_8_bit_register_3_output_pin_7), .S_i(and_63_out),
    .C_i(and_63_out), .C_o(multiplier_29_c_o), .S(multiplier_29_s));
  Multiplier multiplier_30 (
    .A(rising_8_bit_register_1_output_pin_1), .B(rising_8_bit_register_3_output_pin_6),
    .S_i(multiplier_29_s), .C_i(multiplier_37_c_o), .C_o(multiplier_30_c_o), .S(multiplier_30_s));
  Multiplier multiplier_31 (
    .A(rising_8_bit_register_1_output_pin_2), .B(rising_8_bit_register_3_output_pin_5),
    .S_i(multiplier_30_s), .C_i(multiplier_38_c_o), .C_o(multiplier_31_c_o), .S(multiplier_31_s));
  Multiplier multiplier_32 (
    .A(rising_8_bit_register_1_output_pin_3), .B(rising_8_bit_register_3_output_pin_4),
    .S_i(multiplier_31_s), .C_i(multiplier_39_c_o), .C_o(multiplier_32_c_o), .S(multiplier_32_s));
  Multiplier multiplier_33 (
    .A(rising_8_bit_register_1_output_pin_4), .B(rising_8_bit_register_3_output_pin_3),
    .S_i(multiplier_32_s), .C_i(multiplier_40_c_o), .C_o(multiplier_33_c_o), .S(multiplier_33_s));
  Multiplier multiplier_34 (
    .A(rising_8_bit_register_1_output_pin_5), .B(rising_8_bit_register_3_output_pin_2),
    .S_i(multiplier_33_s), .C_i(multiplier_41_c_o), .C_o(multiplier_34_c_o), .S(multiplier_34_s));
  Multiplier multiplier_35 (
    .A(rising_8_bit_register_1_output_pin_6), .B(rising_8_bit_register_3_output_pin_1),
    .S_i(multiplier_34_s), .C_i(multiplier_42_c_o), .C_o(multiplier_35_c_o), .S(multiplier_35_s));
  Multiplier multiplier_36 (
    .A(rising_8_bit_register_1_output_pin_7), .B(rising_8_bit_register_3_output_pin_0),
    .S_i(multiplier_35_s), .C_i(multiplier_43_c_o), .S(multiplier_36_s));  // open: C_o
  Multiplier multiplier_37 (
    .A(rising_8_bit_register_1_output_pin_0), .B(rising_8_bit_register_3_output_pin_6), .S_i(and_63_out),
    .C_i(and_63_out), .C_o(multiplier_37_c_o), .S(multiplier_37_s));
  Multiplier multiplier_38 (
    .A(rising_8_bit_register_1_output_pin_1), .B(rising_8_bit_register_3_output_pin_5),
    .S_i(multiplier_37_s), .C_i(multiplier_44_c_o), .C_o(multiplier_38_c_o), .S(multiplier_38_s));
  Multiplier multiplier_39 (
    .A(rising_8_bit_register_1_output_pin_2), .B(rising_8_bit_register_3_output_pin_4),
    .S_i(multiplier_38_s), .C_i(multiplier_45_c_o), .C_o(multiplier_39_c_o), .S(multiplier_39_s));
  Multiplier multiplier_40 (
    .A(rising_8_bit_register_1_output_pin_3), .B(rising_8_bit_register_3_output_pin_3),
    .S_i(multiplier_39_s), .C_i(multiplier_46_c_o), .C_o(multiplier_40_c_o), .S(multiplier_40_s));
  Multiplier multiplier_41 (
    .A(rising_8_bit_register_1_output_pin_4), .B(rising_8_bit_register_3_output_pin_2),
    .S_i(multiplier_40_s), .C_i(multiplier_47_c_o), .C_o(multiplier_41_c_o), .S(multiplier_41_s));
  Multiplier multiplier_42 (
    .A(rising_8_bit_register_1_output_pin_5), .B(rising_8_bit_register_3_output_pin_1),
    .S_i(multiplier_41_s), .C_i(multiplier_48_c_o), .C_o(multiplier_42_c_o), .S(multiplier_42_s));
  Multiplier multiplier_43 (
    .A(rising_8_bit_register_1_output_pin_6), .B(rising_8_bit_register_3_output_pin_0),
    .S_i(multiplier_42_s), .C_i(multiplier_49_c_o), .C_o(multiplier_43_c_o), .S(multiplier_43_s));
  Multiplier multiplier_44 (
    .A(rising_8_bit_register_1_output_pin_0), .B(rising_8_bit_register_3_output_pin_5), .S_i(and_63_out),
    .C_i(and_63_out), .C_o(multiplier_44_c_o), .S(multiplier_44_s));
  Multiplier multiplier_45 (
    .A(rising_8_bit_register_1_output_pin_1), .B(rising_8_bit_register_3_output_pin_4),
    .S_i(multiplier_44_s), .C_i(multiplier_50_c_o), .C_o(multiplier_45_c_o), .S(multiplier_45_s));
  Multiplier multiplier_46 (
    .A(rising_8_bit_register_1_output_pin_2), .B(rising_8_bit_register_3_output_pin_3),
    .S_i(multiplier_45_s), .C_i(multiplier_51_c_o), .C_o(multiplier_46_c_o), .S(multiplier_46_s));
  Multiplier multiplier_47 (
    .A(rising_8_bit_register_1_output_pin_3), .B(rising_8_bit_register_3_output_pin_2),
    .S_i(multiplier_46_s), .C_i(multiplier_52_c_o), .C_o(multiplier_47_c_o), .S(multiplier_47_s));
  Multiplier multiplier_48 (
    .A(rising_8_bit_register_1_output_pin_4), .B(rising_8_bit_register_3_output_pin_1),
    .S_i(multiplier_47_s), .C_i(multiplier_53_c_o), .C_o(multiplier_48_c_o), .S(multiplier_48_s));
  Multiplier multiplier_49 (
    .A(rising_8_bit_register_1_output_pin_5), .B(rising_8_bit_register_3_output_pin_0),
    .S_i(multiplier_48_s), .C_i(multiplier_54_c_o), .C_o(multiplier_49_c_o), .S(multiplier_49_s));
  Multiplier multiplier_50 (
    .A(rising_8_bit_register_1_output_pin_0), .B(rising_8_bit_register_3_output_pin_4), .S_i(and_63_out),
    .C_i(and_63_out), .C_o(multiplier_50_c_o), .S(multiplier_50_s));
  Multiplier multiplier_51 (
    .A(rising_8_bit_register_1_output_pin_1), .B(rising_8_bit_register_3_output_pin_3),
    .S_i(multiplier_50_s), .C_i(multiplier_55_c_o), .C_o(multiplier_51_c_o), .S(multiplier_51_s));
  Multiplier multiplier_52 (
    .A(rising_8_bit_register_1_output_pin_2), .B(rising_8_bit_register_3_output_pin_2),
    .S_i(multiplier_51_s), .C_i(multiplier_56_c_o), .C_o(multiplier_52_c_o), .S(multiplier_52_s));
  Multiplier multiplier_53 (
    .A(rising_8_bit_register_1_output_pin_3), .B(rising_8_bit_register_3_output_pin_1),
    .S_i(multiplier_52_s), .C_i(multiplier_57_c_o), .C_o(multiplier_53_c_o), .S(multiplier_53_s));
  Multiplier multiplier_54 (
    .A(rising_8_bit_register_1_output_pin_4), .B(rising_8_bit_register_3_output_pin_0),
    .S_i(multiplier_53_s), .C_i(multiplier_58_c_o), .C_o(multiplier_54_c_o), .S(multiplier_54_s));
  Multiplier multiplier_55 (
    .A(rising_8_bit_register_1_output_pin_0), .B(rising_8_bit_register_3_output_pin_3), .S_i(and_63_out),
    .C_i(and_63_out), .C_o(multiplier_55_c_o), .S(multiplier_55_s));
  Multiplier multiplier_56 (
    .A(rising_8_bit_register_1_output_pin_1), .B(rising_8_bit_register_3_output_pin_2),
    .S_i(multiplier_55_s), .C_i(multiplier_59_c_o), .C_o(multiplier_56_c_o), .S(multiplier_56_s));
  Multiplier multiplier_57 (
    .A(rising_8_bit_register_1_output_pin_2), .B(rising_8_bit_register_3_output_pin_1),
    .S_i(multiplier_56_s), .C_i(multiplier_60_c_o), .C_o(multiplier_57_c_o), .S(multiplier_57_s));
  Multiplier multiplier_58 (
    .A(rising_8_bit_register_1_output_pin_3), .B(rising_8_bit_register_3_output_pin_0),
    .S_i(multiplier_57_s), .C_i(multiplier_61_c_o), .C_o(multiplier_58_c_o), .S(multiplier_58_s));
  Multiplier multiplier_59 (
    .A(rising_8_bit_register_1_output_pin_0), .B(rising_8_bit_register_3_output_pin_2), .S_i(and_63_out),
    .C_i(and_63_out), .C_o(multiplier_59_c_o), .S(multiplier_59_s));
  Multiplier multiplier_60 (
    .A(rising_8_bit_register_1_output_pin_1), .B(rising_8_bit_register_3_output_pin_1),
    .S_i(multiplier_59_s), .C_i(multiplier_62_c_o), .C_o(multiplier_60_c_o), .S(multiplier_60_s));
  Multiplier multiplier_61 (
    .A(rising_8_bit_register_1_output_pin_2), .B(rising_8_bit_register_3_output_pin_0),
    .S_i(multiplier_60_s), .C_i(multiplier_63_c_o), .C_o(multiplier_61_c_o), .S(multiplier_61_s));
  Multiplier multiplier_62 (
    .A(rising_8_bit_register_1_output_pin_0), .B(rising_8_bit_register_3_output_pin_1), .S_i(and_63_out),
    .C_i(and_63_out), .C_o(multiplier_62_c_o), .S(multiplier_62_s));
  Multiplier multiplier_63 (
    .A(rising_8_bit_register_1_output_pin_1), .B(rising_8_bit_register_3_output_pin_0),
    .S_i(multiplier_62_s), .C_i(multiplier_64_c_o), .C_o(multiplier_63_c_o), .S(multiplier_63_s));
  Multiplier multiplier_64 (
    .A(rising_8_bit_register_1_output_pin_0), .B(rising_8_bit_register_3_output_pin_0), .S_i(and_63_out),
    .C_i(and_63_out), .C_o(multiplier_64_c_o), .S(multiplier_64_s));

  // Notes on the sheet:
  //   Legend for Control Bits
  //   0 0 0 ADD
  //   0 0 1 BEQ
  //   0 1 0 BNQ
  //   0 1 1 SUB
  //   1 X X MULT
  //   BEQ and BNQ output:
  //   True: 1 0 0 0 0 0 0 0 
  //   False: 0 0 0 0 0 0 0 0
  //   Left Register
endmodule

module Multiplier (
  input  A,
  input  B,
  input  S_i,
  input  C_i,
  output C_o,
  output S
);

  wire and_1_out, and_2_out, and_3_out, xor_1_out;

  and and_1 (and_1_out, S_i, and_2_out);
  or or_1 (C_o, and_1_out, and_3_out);
  and and_2 (and_2_out, A, B);
  and and_3 (and_3_out, C_i, xor_1_out);
  xor xor_1 (xor_1_out, S_i, and_2_out);
  xor xor_2 (S, xor_1_out, C_i);
endmodule
