// Logisim project CPU.circ as structural Verilog: 2 circuits, main circuit CPU
module CPU (
  input  ON_OFF_BUTTON,
  input  ROM_on_off,
  output [2:0] TickCount,
  output Mode,
  output [3:0] Address,
  output Status
);

  wire _0_out, _1_out, _2_out, _3_out, _4_out, _5_out, _6_out, _7_out, _8_out, _9_out, and_1_out, Clock_out,
       control_unit_1_a_s, control_unit_1_alu0, control_unit_1_alu1, control_unit_1_alu2,
       control_unit_1_beqbnq, control_unit_1_d1, control_unit_1_d2, control_unit_1_disp, control_unit_1_ir,
       control_unit_1_l, control_unit_1_mar, control_unit_1_mbr, control_unit_1_mxcben,
       control_unit_1_mxd1d2sel, control_unit_1_mxmarsel, control_unit_1_mxmbr, control_unit_1_mxrlsel,
       control_unit_1_pc, control_unit_1_r, control_unit_1_ram, control_unit_1_reset, main_2__0a, main_2__0b,
       main_2__0c, main_2__0d, main_2__0e, main_2__0f, main_2__0g, main_2__1a, main_2__1b, main_2__1c,
       main_2__1d, main_2__1e, main_2__1f, main_2__1g, main_2__2a, main_2__2b, main_2__2c, main_2__2d,
       main_2__2e, main_2__2f, main_2__2g, or_1_out, or_2_out, rom_1_romend;
  wire [1:0] control_unit_1_dxcbsel, control_unit_1_dxsbsel, control_unit_1_mxcbs, control_unit_1_mxsbsel;
  wire [3:0] IR_output_pin_0, multiplexer_2_out, multiplexer_7_out, program_counter_1_tomar0, rom_1_address;
  wire [7:0] bit_extender_1_out_8, demultiplexer_1_out1, demultiplexer_1_out2, demultiplexer_1_out3,
       demultiplexer_2_out0, demultiplexer_2_out1, demultiplexer_3_out1, demultiplexer_3_out2,
       demultiplexer_3_out3, demultiplexer_4_out0, demultiplexer_4_out1, main_1__0_2, main_3_a0,
       MBR_output_pin_0, multiplexer_1_out, multiplexer_3_out, multiplexer_4_out, multiplexer_5_out,
       multiplexer_6_out, R1_output_pin_7, R2_output_pin_7, ram_1_to_mbr0, rom_1_data;
  wire [7:4] IR_output_pin_4;

  Clock Clock (.out(Clock_out));
  Button _7 (.out(_7_out));
  Button _9 (.out(_9_out));
  Button _8 (.out(_8_out));
  Button _5 (.out(_5_out));
  Button _4 (.out(_4_out));
  Button _6 (.out(_6_out));
  Button _1 (.out(_1_out));
  Button _2 (.out(_2_out));
  Button _3 (.out(_3_out));
  Button _0 (.out(_0_out));
  _7_Segment_Display u_7_segment_display_1 (
    .g(main_2__2g), .f(main_2__2f), .a(main_2__2a), .b(main_2__2b), .e(main_2__2e), .d(main_2__2d),
    .c(main_2__2c));  // open: dp
  KeyBuffer_main main_1 (
    ._0(_0_out), ._1(_1_out), ._2(_2_out), ._3(_3_out), ._4(_4_out), ._5(_5_out), ._6(_6_out), ._7(_7_out),
    ._8(_8_out), ._9(_9_out), ._7_2(main_1__0_2[7]), ._6_2(main_1__0_2[6]), ._5_2(main_1__0_2[5]),
    ._4_2(main_1__0_2[4]), ._3_2(main_1__0_2[3]), ._2_2(main_1__0_2[2]), ._1_2(main_1__0_2[1]),
    ._0_2(main_1__0_2[0]), .RESET(control_unit_1_reset));
  _7_Segment_Display u_7_segment_display_2 (
    .g(main_2__1g), .f(main_2__1f), .a(main_2__1a), .b(main_2__1b), .e(main_2__1e), .d(main_2__1d),
    .c(main_2__1c));  // open: dp
  or or_1 (or_1_out, control_unit_1_ram, and_1_out);
  RAM ram_1 (
    .R_W(or_2_out), .Clock(Clock_out), .From_MBR_0(multiplexer_1_out[0]), .From_MBR_1(multiplexer_1_out[1]),
    .From_MBR_2(multiplexer_1_out[2]), .From_MBR_3(multiplexer_1_out[3]), .From_MBR_4(multiplexer_1_out[4]),
    .From_MBR_5(multiplexer_1_out[5]), .From_MBR_6(multiplexer_1_out[6]), .CU_Enabler(or_1_out),
    .From_MBR_7(multiplexer_1_out[7]), .To_MBR_7(ram_1_to_mbr0[7]), .To_MBR6(ram_1_to_mbr0[6]),
    .To_MBR5(ram_1_to_mbr0[5]), .To_MBR4(ram_1_to_mbr0[4]), .To_MBR3(ram_1_to_mbr0[3]),
    .To_MBR2(ram_1_to_mbr0[2]), .To_MBR1(ram_1_to_mbr0[1]), .To_MBR0(ram_1_to_mbr0[0]),
    .MAR_0(multiplexer_2_out[0]), .MAR_1(multiplexer_2_out[1]), .MAR_2(multiplexer_2_out[2]),
    .MAR_3(multiplexer_2_out[3]), .RESET(control_unit_1_reset));
  Display_main main_2 (
    ._2a(main_2__2a), ._2b(main_2__2b), ._2c(main_2__2c), ._2d(main_2__2d), ._2e(main_2__2e),
    ._2f(main_2__2f), ._2g(main_2__2g), ._0a(main_2__0a), ._0b(main_2__0b), ._0c(main_2__0c),
    ._0d(main_2__0d), ._0e(main_2__0e), ._0f(main_2__0f), ._0g(main_2__0g), ._1a(main_2__1a),
    ._1b(main_2__1b), ._1c(main_2__1c), ._1d(main_2__1d), ._1e(main_2__1e), ._1f(main_2__1f),
    ._1g(main_2__1g), .Clock(Clock_out), .Enabler(control_unit_1_disp), ._7(demultiplexer_1_out3[7]),
    ._6(demultiplexer_1_out3[6]), ._5(demultiplexer_1_out3[5]), ._4(demultiplexer_1_out3[4]),
    ._3(demultiplexer_1_out3[3]), ._2(demultiplexer_1_out3[2]), ._1(demultiplexer_1_out3[1]),
    ._0(demultiplexer_1_out3[0]), .RESET(control_unit_1_reset));
  _7_Segment_Display u_7_segment_display_3 (
    .g(main_2__0g), .f(main_2__0f), .a(main_2__0a), .b(main_2__0b), .e(main_2__0e), .d(main_2__0d),
    .c(main_2__0c));  // open: dp
  and and_1 (and_1_out, ROM_on_off, ~rom_1_romend);  // AND_Gate
  or or_2 (or_2_out, Mode, and_1_out);
  Multiplexer #(.width(8), .enable("false")) multiplexer_1 (
    .in0(demultiplexer_1_out2), .in1(rom_1_data), .out(multiplexer_1_out), .sel(and_1_out));
  Multiplexer #(.width(4), .enable("false")) multiplexer_2 (
    .in0(Address), .in1(rom_1_address), .out(multiplexer_2_out), .sel(and_1_out));
  ROM rom_1 (.Enabler(and_1_out), .Data(rom_1_data), .Address(rom_1_address), .ROMend(rom_1_romend), .Clock(Clock_out));
  Multiplexer #(.select(2), .width(8), .enable("false")) multiplexer_3 (
    .in0({8{1'b0}}), .in1(MBR_output_pin_0), .in2(ram_1_to_mbr0), .in3(main_1__0_2), .out(multiplexer_3_out),
    .sel(control_unit_1_mxsbsel));
  Demultiplexer #(.select(2), .width(8), .enable("false")) demultiplexer_1 (
    .out1(demultiplexer_1_out1), .out2(demultiplexer_1_out2), .out3(demultiplexer_1_out3),
    .in(multiplexer_3_out), .sel(control_unit_1_dxsbsel));  // open: out0
  Multiplexer #(.width(8), .enable("false")) multiplexer_4 (
    .in0(R1_output_pin_7), .in1(R2_output_pin_7), .out(multiplexer_4_out), .sel(control_unit_1_mxd1d2sel));
  Multiplexer #(.width(8), .disabled(0), .enable("false")) multiplexer_5 (
    .in0(demultiplexer_1_out1), .in1(demultiplexer_3_out1), .out(multiplexer_5_out),
    .sel(control_unit_1_mxmbr));
  Multiplexer #(.select(2), .width(8)) multiplexer_6 (
    .in0(MBR_output_pin_0), .in1(multiplexer_4_out), .in2(main_3_a0), .in3(bit_extender_1_out_8),
    .out(multiplexer_6_out), .sel(control_unit_1_mxcbs), .en(control_unit_1_mxcben));
  Rising_4_Bit_Register MAR (
    .Input_Pin_0(multiplexer_7_out[0]), .Input_Pin_1(multiplexer_7_out[1]),
    .Input_Pin_2(multiplexer_7_out[2]), .Input_Pin_3(multiplexer_7_out[3]), .Output_Pin_0(Address[0]),
    .Output_Pin_1(Address[1]), .Output_Pin_2(Address[2]), .Output_Pin_3(Address[3]),
    .Enabler(control_unit_1_mar), .Clock(Clock_out), .RESET(control_unit_1_reset));
  Rising_8_Bit_Register R1 (
    .Enabler(control_unit_1_d1), .Clock(Clock_out), .Input_Pin_0(demultiplexer_2_out0[7]),
    .Input_Pin_1(demultiplexer_2_out0[6]), .Input_Pin_2(demultiplexer_2_out0[5]),
    .Input_Pin_3(demultiplexer_2_out0[4]), .Input_Pin_4(demultiplexer_2_out0[3]),
    .Input_Pin_5(demultiplexer_2_out0[2]), .Input_Pin_6(demultiplexer_2_out0[1]),
    .Input_Pin_7(demultiplexer_2_out0[0]), .Output_Pin_0(R1_output_pin_7[7]),
    .Output_Pin_1(R1_output_pin_7[6]), .Output_Pin_2(R1_output_pin_7[5]), .Output_Pin_3(R1_output_pin_7[4]),
    .Output_Pin_4(R1_output_pin_7[3]), .Output_Pin_5(R1_output_pin_7[2]), .Output_Pin_6(R1_output_pin_7[1]),
    .Output_Pin_7(R1_output_pin_7[0]), .RESET(control_unit_1_reset));
  Rising_8_Bit_Register R2 (
    .Enabler(control_unit_1_d2), .Clock(Clock_out), .Input_Pin_0(demultiplexer_2_out1[7]),
    .Input_Pin_1(demultiplexer_2_out1[6]), .Input_Pin_2(demultiplexer_2_out1[5]),
    .Input_Pin_3(demultiplexer_2_out1[4]), .Input_Pin_4(demultiplexer_2_out1[3]),
    .Input_Pin_5(demultiplexer_2_out1[2]), .Input_Pin_6(demultiplexer_2_out1[1]),
    .Input_Pin_7(demultiplexer_2_out1[0]), .Output_Pin_0(R2_output_pin_7[7]),
    .Output_Pin_1(R2_output_pin_7[6]), .Output_Pin_2(R2_output_pin_7[5]), .Output_Pin_3(R2_output_pin_7[4]),
    .Output_Pin_4(R2_output_pin_7[3]), .Output_Pin_5(R2_output_pin_7[2]), .Output_Pin_6(R2_output_pin_7[1]),
    .Output_Pin_7(R2_output_pin_7[0]), .RESET(control_unit_1_reset));
  Multiplexer #(.width(4), .disabled(0), .enable("false")) multiplexer_7 (
    .in0(program_counter_1_tomar0), .in1(IR_output_pin_0), .out(multiplexer_7_out),
    .sel(control_unit_1_mxmarsel));
  Rising_8_Bit_Register MBR (
    .Enabler(control_unit_1_mbr), .Clock(Clock_out), .Input_Pin_0(multiplexer_5_out[0]),
    .Input_Pin_1(multiplexer_5_out[1]), .Input_Pin_2(multiplexer_5_out[2]),
    .Input_Pin_3(multiplexer_5_out[3]), .Input_Pin_4(multiplexer_5_out[4]),
    .Input_Pin_5(multiplexer_5_out[5]), .Input_Pin_6(multiplexer_5_out[6]),
    .Input_Pin_7(multiplexer_5_out[7]), .Output_Pin_0(MBR_output_pin_0[0]),
    .Output_Pin_1(MBR_output_pin_0[1]), .Output_Pin_2(MBR_output_pin_0[2]),
    .Output_Pin_3(MBR_output_pin_0[3]), .Output_Pin_4(MBR_output_pin_0[4]),
    .Output_Pin_5(MBR_output_pin_0[5]), .Output_Pin_6(MBR_output_pin_0[6]),
    .Output_Pin_7(MBR_output_pin_0[7]), .RESET(control_unit_1_reset));
  Demultiplexer #(.width(8), .enable("false")) demultiplexer_2 (
    .out0(demultiplexer_2_out0), .out1(demultiplexer_2_out1), .in(demultiplexer_3_out2),
    .sel(control_unit_1_mxd1d2sel));
  Demultiplexer #(.select(2), .width(8), .enable("false")) demultiplexer_3 (
    .out1(demultiplexer_3_out1), .out2(demultiplexer_3_out2), .out3(demultiplexer_3_out3),
    .in(multiplexer_6_out), .sel(control_unit_1_dxcbsel));  // open: out0
  ALU_main main_3 (
    .Clock(Clock_out), .L_Enabler(control_unit_1_l), .R_Enabler(control_unit_1_r),
    .Answer_Enabler(control_unit_1_a_s), .Status_Enabler(control_unit_1_a_s), .C0(control_unit_1_alu0),
    .C1(control_unit_1_alu1), .Status(Status), .L7(demultiplexer_4_out0[7]), .L6(demultiplexer_4_out0[6]),
    .L5(demultiplexer_4_out0[5]), .L4(demultiplexer_4_out0[4]), .L3(demultiplexer_4_out0[3]),
    .L2(demultiplexer_4_out0[2]), .L1(demultiplexer_4_out0[1]), .L0(demultiplexer_4_out0[0]),
    .R7(demultiplexer_4_out1[7]), .R6(demultiplexer_4_out1[6]), .R5(demultiplexer_4_out1[5]),
    .R4(demultiplexer_4_out1[4]), .R3(demultiplexer_4_out1[3]), .R2(demultiplexer_4_out1[2]),
    .R1(demultiplexer_4_out1[1]), .R0(demultiplexer_4_out1[0]), .A7(main_3_a0[7]), .A6(main_3_a0[6]),
    .A5(main_3_a0[5]), .A4(main_3_a0[4]), .A3(main_3_a0[3]), .A2(main_3_a0[2]), .A1(main_3_a0[1]),
    .A0(main_3_a0[0]), .C2(control_unit_1_alu2), .RESET(control_unit_1_reset));
  Program_Counter program_counter_1 (
    .Enabler(control_unit_1_pc), .Clock(Clock_out), .Zero(control_unit_1_reset),
    .BEQ_or_BNQ(control_unit_1_beqbnq), .readFromBranch(Status), .toMAR0(program_counter_1_tomar0[0]),
    .toMAR1(program_counter_1_tomar0[1]), .toMAR2(program_counter_1_tomar0[2]),
    .toMAR3(program_counter_1_tomar0[3]), .addresFromBranch(IR_output_pin_0));
  Control_Unit control_unit_1 (
    .ALU0(control_unit_1_alu0), .MAR(control_unit_1_mar), .Mode(Mode), .RAM(control_unit_1_ram),
    .MBR(control_unit_1_mbr), .D1(control_unit_1_d1), .L(control_unit_1_l), .R(control_unit_1_r),
    .A_S(control_unit_1_a_s), .PC(control_unit_1_pc), .DISP(control_unit_1_disp), .b4(IR_output_pin_4[4]),
    .b5(IR_output_pin_4[5]), .b6(IR_output_pin_4[6]), .b7(IR_output_pin_4[7]), .IR(control_unit_1_ir),
    .b3(IR_output_pin_0[3]), .b2(IR_output_pin_0[2]), .b1(IR_output_pin_0[1]), .b0(IR_output_pin_0[0]),
    .ON_OFF(ON_OFF_BUTTON), .ALU2(control_unit_1_alu2), .ALU1(control_unit_1_alu1),
    .RESET(control_unit_1_reset), .Clock(Clock_out), .ROMstart(and_1_out), .MXSBsel(control_unit_1_mxsbsel),
    .MXCBen(control_unit_1_mxcben), .DXSBsel(control_unit_1_dxsbsel), .DXCBsel(control_unit_1_dxcbsel),
    .MXMARsel(control_unit_1_mxmarsel), .MXRLsel(control_unit_1_mxrlsel),
    .MXD1D2sel(control_unit_1_mxd1d2sel), .MXmbr(control_unit_1_mxmbr), .BEQBNQ(control_unit_1_beqbnq),
    .out_13(TickCount), .D2(control_unit_1_d2), .MXCBs(control_unit_1_mxcbs), .BNQ_BNE_Ena_bler(Status));
  Demultiplexer #(.width(8), .enable("false")) demultiplexer_4 (
    .out0(demultiplexer_4_out0), .out1(demultiplexer_4_out1), .in(demultiplexer_3_out3),
    .sel(control_unit_1_mxrlsel));
  Falling_8_bit_Register IR (
    .Input_Pin_0(MBR_output_pin_0[0]), .Input_Pin_1(MBR_output_pin_0[1]), .Input_Pin_2(MBR_output_pin_0[2]),
    .Input_Pin_3(MBR_output_pin_0[3]), .Input_Pin_4(MBR_output_pin_0[4]), .Input_Pin_5(MBR_output_pin_0[5]),
    .Input_Pin_6(MBR_output_pin_0[6]), .Input_Pin_7(MBR_output_pin_0[7]), .Output_Pin_0(IR_output_pin_0[0]),
    .Output_Pin_1(IR_output_pin_0[1]), .Output_Pin_2(IR_output_pin_0[2]), .Output_Pin_3(IR_output_pin_0[3]),
    .Output_Pin_4(IR_output_pin_4[4]), .Output_Pin_5(IR_output_pin_4[5]), .Output_Pin_6(IR_output_pin_4[6]),
    .Output_Pin_7(IR_output_pin_4[7]), .Enabler(control_unit_1_ir), .Clock(Clock_out),
    .RESET(control_unit_1_reset));
  Bit_Extender bit_extender_1 (
    .in_1(IR_output_pin_0[3]), .in_2(IR_output_pin_0[2]), .in_3(IR_output_pin_0[1]),
    .in_4(IR_output_pin_0[0]), .out_5(bit_extender_1_out_8[3]), .out_6(bit_extender_1_out_8[2]),
    .out_7(bit_extender_1_out_8[1]), .out_8(bit_extender_1_out_8[0]), .out_9(bit_extender_1_out_8[4]),
    .out_10(bit_extender_1_out_8[5]), .out_11(bit_extender_1_out_8[7]), .out_12(bit_extender_1_out_8[6]));

  // Other names for the same wires on the sheet: ON_OFF = ON_OFF_BUTTON

  // Notes on the sheet:
  //   Out
  //   In
  //   MODE BUS
  //   SYSTEM BUS
  //   DATA BUS
  //   ADDRESS BUS
  //   SYSTEM BUS
  //   CPU BUS
  //   Left
  //   Status
  //   A
  //   Right
endmodule

// BIT EXTENDER
module Bit_Extender (
  input  in_1,
  input  in_2,
  input  in_3,
  input  in_4,
  output out_5,
  output out_6,
  output out_7,
  output out_8,
  output out_9,
  output out_10,
  output out_11,
  output out_12
);

  wire not_1_out;

  not not_1 (not_1_out, in_4);
  and and_1 (out_5, not_1_out, in_4);

  assign out_6 = in_2;
  assign out_7 = in_3;
  assign out_8 = in_4;
  assign out_9 = out_5;
  assign out_10 = out_5;
  assign out_11 = out_5;
  assign out_12 = out_5;
endmodule
