// Logisim project CU_Counter.circ as structural Verilog: 1 circuit, main circuit main
// CU Counter
module main (
  input  Clock,
  input  RESET,
  output [2:0] Counter
);

  wire [2:0] adder_1_out;

  D_Flip_Flop d_ff_1 (.clk(Clock), .D(adder_1_out[0]), .Q(Counter[0]), .reset(RESET));  // open: Qn, preset, en
  D_Flip_Flop d_ff_2 (.clk(Clock), .D(adder_1_out[1]), .Q(Counter[1]), .reset(RESET));  // open: Qn, preset, en
  D_Flip_Flop d_ff_3 (.clk(Clock), .D(adder_1_out[2]), .Q(Counter[2]), .reset(RESET));  // open: Qn, preset, en
  Adder #(.width(3)) adder_1 (.a(Counter), .b(3'b001), .out(adder_1_out));  // open: cin, cout
endmodule
