// Logisim project ControlUnit.circ as structural Verilog: 14 circuits, main circuit Control Unit
// CONTROL UNIT
module Control_Unit (
  input  Clock,
  input  b7,
  input  b6,
  input  b5,
  input  b4,
  input  b3,
  input  b2,
  input  b1,
  input  b0,
  input  ON_OFF,
  input  ROMstart,
  input  BNQ_BNE_Ena_bler,
  output [2:0] out_13,
  output RESET,
  output ALU2,
  output ALU1,
  output ALU0,
  output BEQBNQ,
  output IR,
  output RAM,
  output Mode,
  output MAR,
  output MBR,
  output D1,
  output D2,
  output L,
  output R,
  output A_S,
  output PC,
  output DISP,
  output MXmbr,
  output MXMARsel,
  output MXRLsel,
  output MXD1D2sel,
  output MXCBen,
  output [1:0] DXCBsel,
  output [1:0] MXSBsel,
  output [1:0] DXSBsel,
  output [1:0] MXCBs
);

  wire bus_controls_1_cb_enabler, d1_d2_1_d1, d1_d2_1_d2, decoder_1_out0, decoder_1_out1, decoder_1_out2,
       decoder_1_out3, decoder_1_out4, decoder_1_out5, decoder_1_out6, decoder_1_out7, disp_1_disp, ir_1_ir,
       l_r_a_s_1_a_s, l_r_a_s_1_l, l_r_a_s_1_r, mar_1_mar, mbr_1_mbr, mode_1_mode, or_1_out,
       other_mux_controls_1_d1_d2_select, other_mux_controls_1_mux_mar_enabler, other_mux_controls_1_mux_mbr,
       other_mux_controls_1_r_l_select, pc_1_pc, ram_1_ram, STOP_out;
  wire [1:0] bus_controls_1_dmx_cb_select, bus_controls_1_dmx_sb_select, bus_controls_1_mux_cb_select,
       bus_controls_1_mux_sbd_select;

  not not_1 (RESET, ON_OFF);
  Decoder #(.select(3), .enable("false")) decoder_1 (
    .out0(decoder_1_out0), .out1(decoder_1_out1), .out2(decoder_1_out2), .out3(decoder_1_out3),
    .out4(decoder_1_out4), .out5(decoder_1_out5), .out6(decoder_1_out6), .out7(decoder_1_out7), .sel(out_13));
  CU_Counter_main main_1 (.Clock(Clock), .RESET(ROMstart), .Counter(out_13));
  and STOP (STOP_out, b7, b6, b5, b4, b3, b2, b1, b0);
  or or_1 (or_1_out, STOP_out, ~ON_OFF, ROMstart);  // OR_Gate
  ALU210 alu210_1 (
    .b7(b7), .b6(b6), .b5(b5), .b3(b3), .Clock(Clock), .T4(decoder_1_out5), .T5(decoder_1_out6), .ALU1(ALU1),
    .ALU2(ALU2), .ALU0(ALU0), .T6(decoder_1_out7));
  BEQ_BNQ beq_bnq_1 (
    .ALUc1(ALU1), .ALUc0(ALU0), .BEQ_BNQ(BEQBNQ), .clock(Clock), .t6(decoder_1_out7), .t5(decoder_1_out6));
  IR ir_1 (.T2(decoder_1_out3), .IR(ir_1_ir));
  and and_1 (IR, ~or_1_out, ir_1_ir);  // AND_Gate
  RAM ram_1 (
    .b7(b7), .b6(b6), .b5(b5), .Clock(Clock), .T0(decoder_1_out1), .T3(decoder_1_out4), .T6(decoder_1_out7),
    .RAM(ram_1_ram), .T5(decoder_1_out6), .T4(decoder_1_out5), .T1(decoder_1_out2));
  and and_2 (RAM, ~or_1_out, ram_1_ram);  // AND_Gate
  Mode mode_1 (
    .b7(b7), .b6(b6), .b5(b5), .T6(decoder_1_out7), .T5(decoder_1_out6), .Mode(mode_1_mode), .Clock(Clock),
    .T4(decoder_1_out5));
  and and_3 (Mode, ~or_1_out, mode_1_mode);  // AND_Gate
  MAR mar_1 (
    .b7(b7), .b6(b6), .b5(b5), .T3(decoder_1_out4), .MAR(mar_1_mar), .clock(Clock), .T0(decoder_1_out1),
    .T6(decoder_1_out7), .T2(decoder_1_out3), .T_1(decoder_1_out0));
  and and_4 (MAR, ~or_1_out, mar_1_mar);  // AND_Gate
  MBR mbr_1 (
    .b7(b7), .b6(b6), .b5(b5), .Clock(Clock), .T2(decoder_1_out3), .T3(decoder_1_out4), .T4(decoder_1_out5),
    .T5(decoder_1_out6), .MBR(mbr_1_mbr), .T1(decoder_1_out2));
  and and_5 (MBR, ~or_1_out, mbr_1_mbr);  // AND_Gate
  D1__D2 d1_d2_1 (
    .b7(b7), .b6(b6), .b5(b5), .T6(decoder_1_out7), .D1(d1_d2_1_d1), .Clock(Clock), .T5(decoder_1_out6),
    .b4(b4), .D2(d1_d2_1_d2));
  and and_6 (D2, ~or_1_out, d1_d2_1_d2);  // AND_Gate
  and and_7 (D1, ~or_1_out, d1_d2_1_d1);  // AND_Gate
  L__R__A__S l_r_a_s_1 (
    .b7(b7), .b6(b6), .b5(b5), .Clock(Clock), .T3(decoder_1_out4), .T4(decoder_1_out5), .T5(decoder_1_out6),
    .L(l_r_a_s_1_l), .R(l_r_a_s_1_r), .A_S(l_r_a_s_1_a_s), .T2(decoder_1_out3), .b4(b4));
  and and_8 (R, ~or_1_out, l_r_a_s_1_r);  // AND_Gate
  and and_9 (L, ~or_1_out, l_r_a_s_1_l);  // AND_Gate
  PC pc_1 (
    .b7(b7), .b6(b6), .b5(b5), .Clock(Clock), .T6(decoder_1_out7), .PC(pc_1_pc), .T5(decoder_1_out6),
    .T0(decoder_1_out0), .readFromBranch(BNQ_BNE_Ena_bler));
  and and_10 (PC, ~or_1_out, pc_1_pc);  // AND_Gate
  and and_11 (A_S, ~or_1_out, l_r_a_s_1_a_s);  // AND_Gate
  DISP disp_1 (.b7(b7), .b6(b6), .b5(b5), .Clock(Clock), .T6(decoder_1_out7), .DISP(disp_1_disp), .T5(decoder_1_out6));
  and and_12 (DISP, ~or_1_out, disp_1_disp);  // AND_Gate
  Multiplexer #(.width(2), .enable("false")) multiplexer_1 (
    .in0(bus_controls_1_mux_sbd_select), .in1(2'b00), .out(MXSBsel), .sel(or_1_out));
  Bus_Controls bus_controls_1 (
    .b7(b7), .b6(b6), .b5(b5), .b3(b3), .b2(b2), .b1(b1), .b0(b0), .Clock(Clock), .T2(decoder_1_out3),
    .T3(decoder_1_out4), .T4(decoder_1_out5), .T5(decoder_1_out6), .T6(decoder_1_out7),
    .MUX_SBD_Select(bus_controls_1_mux_sbd_select), .DMX_SB_Select(bus_controls_1_dmx_sb_select),
    .CB_Enabler(bus_controls_1_cb_enabler), .MUX_CB_Select(bus_controls_1_mux_cb_select),
    .DMX_CB_Select(bus_controls_1_dmx_cb_select), .T1(decoder_1_out2));
  and and_13 (MXCBen, ~or_1_out, bus_controls_1_cb_enabler);  // AND_Gate
  Multiplexer #(.width(2), .enable("false")) multiplexer_2 (
    .in0(bus_controls_1_mux_cb_select), .in1(2'b00), .out(MXCBs), .sel(or_1_out));
  Multiplexer #(.width(2), .enable("false")) multiplexer_3 (
    .in0(bus_controls_1_dmx_sb_select), .in1(2'b00), .out(DXSBsel), .sel(or_1_out));
  Other_MUX_Controls other_mux_controls_1 (
    .b7(b7), .b6(b6), .b5(b5), .b3(b3), .b2(b2), .b1(b1), .b0(b0), .Clock(Clock), .T3(decoder_1_out4),
    .T4(decoder_1_out5), .MUX_MAR_Enabler(other_mux_controls_1_mux_mar_enabler),
    .R_L_Select(other_mux_controls_1_r_l_select), .D1_D2_Select(other_mux_controls_1_d1_d2_select),
    .MUX_MBR(other_mux_controls_1_mux_mbr), .b4(b4), .T2(decoder_1_out3), .T6(decoder_1_out7),
    .T5(decoder_1_out6));
  Multiplexer #(.width(2), .enable("false")) multiplexer_4 (
    .in0(bus_controls_1_dmx_cb_select), .in1(2'b00), .out(DXCBsel), .sel(or_1_out));
  and and_14 (MXMARsel, ~or_1_out, other_mux_controls_1_mux_mar_enabler);  // AND_Gate
  and and_15 (MXD1D2sel, ~or_1_out, other_mux_controls_1_d1_d2_select);  // AND_Gate
  and and_16 (MXRLsel, ~or_1_out, other_mux_controls_1_r_l_select);  // AND_Gate
  and and_17 (MXmbr, ~or_1_out, other_mux_controls_1_mux_mbr);  // AND_Gate
endmodule

module IR (
  input  T2,
  output IR
);


  assign IR = T2;
endmodule

module MAR (
  input  T_1,
  input  T0,
  input  T2,
  input  T3,
  input  T6,
  input  b7,
  input  b6,
  input  b5,
  input  clock,
  output MAR
);

  wire _100___t3_out, _100_out, _101_out, or_2_out, t0___c1_2_out, t0___c1_out, t2___c0____100_101_out,
       t6___c0_out;

  and _100___t3 (_100___t3_out, clock, b7, ~b6, ~b5, T3);  // AND_Gate
  and t0___c1 (t0___c1_out, ~clock, T_1);  // AND_Gate
  and t0___c1_2 (t0___c1_2_out, clock, T0);
  or or_1 (MAR, _100___t3_out, t0___c1_2_out, t0___c1_out, t6___c0_out, t2___c0____100_101_out);
  and t6___c0 (t6___c0_out, ~clock, T6);  // AND_Gate
  and _100 (_100_out, b7, ~b6, ~b5);  // AND_Gate
  or or_2 (or_2_out, _100_out, _101_out);
  and t2___c0____100_101 (t2___c0____100_101_out, ~clock, T2, or_2_out);  // AND_Gate
  and _101 (_101_out, b7, ~b6, b5);  // AND_Gate
endmodule

module RAM (
  input  T0,
  input  T1,
  input  T3,
  input  T4,
  input  T5,
  input  T6,
  input  b7,
  input  b6,
  input  b5,
  input  Clock,
  output RAM
);

  wire _100___t3_out, _100___t4___c1_out, _100_out, _101___t5_out, _101_out, c1___t1_out, c1___t6___101_out,
       t4___c0___101_out;

  and c1___t1 (c1___t1_out, Clock, T1);
  or or_1 (RAM, T0, c1___t1_out, _100___t3_out, _100___t4___c1_out, _101___t5_out, c1___t6___101_out, t4___c0___101_out);
  and _100 (_100_out, b7, ~b6, ~b5);  // AND_Gate
  and _101 (_101_out, b7, ~b6, b5);  // AND_Gate
  and _100___t3 (_100___t3_out, _100_out, T3);
  and _100___t4___c1 (_100___t4___c1_out, _100_out, Clock, T4);
  and _101___t5 (_101___t5_out, _101_out, T5);
  and c1___t6___101 (c1___t6___101_out, Clock, T6, _101_out);
  and t4___c0___101 (t4___c0___101_out, ~Clock, T4, _101_out);  // AND_Gate
endmodule

module MBR (
  input  T1,
  input  T2,
  input  T3,
  input  T4,
  input  T5,
  input  b7,
  input  b6,
  input  b5,
  input  Clock,
  output MBR
);

  wire _100_out, _101_out, _110_out, _111_out, and_1_out, and_2_out, and_3_out, and_4_out, and_5_out,
       and_6_out, and_7_out, and_8_out, and_9_out, and_10_out, or_2_out, or_3_out, or_4_out, or_5_out;

  and and_1 (and_1_out, Clock, T2);
  and and_2 (and_2_out, ~Clock, T1);  // AND_Gate
  and _100 (_100_out, b7, ~b6, ~b5);  // AND_Gate
  or or_1 (MBR, and_2_out, and_1_out, and_6_out, and_10_out);
  and _101 (_101_out, b7, ~b6, b5);  // AND_Gate
  and _110 (_110_out, b7, b6, ~b5);  // AND_Gate
  and _111 (_111_out, b7, b6, b5);
  and and_3 (and_3_out, _111_out, T3);
  or or_2 (or_2_out, _100_out, _110_out);
  and and_4 (and_4_out, or_2_out, T5);
  and and_5 (and_5_out, T4, _101_out);
  or or_3 (or_3_out, and_3_out, and_5_out, and_4_out);
  and and_6 (and_6_out, Clock, or_3_out);
  and and_7 (and_7_out, T2, _111_out);
  or or_4 (or_4_out, _100_out, _110_out);
  and and_8 (and_8_out, or_4_out, T4);
  and and_9 (and_9_out, _101_out, T3);
  or or_5 (or_5_out, and_7_out, and_9_out, and_8_out);
  and and_10 (and_10_out, ~Clock, or_5_out);  // AND_Gate
endmodule

// D1 / D2
module D1__D2 (
  input  T5,
  input  T6,
  input  b7,
  input  b6,
  input  b5,
  input  b4,
  input  Clock,
  output D1,
  output D2
);

  wire _000_out, _011_out, _100_out, _110_out, c1___others_out, c1___t5___all_out, or_1_out, or_2_out;

  and _000 (_000_out, ~b7, ~b6, ~b5);  // AND_Gate
  and _011 (_011_out, ~b7, b6, b5);  // AND_Gate
  and _100 (_100_out, b7, ~b6, ~b5);  // AND_Gate
  and _110 (_110_out, b7, b6, ~b5);  // AND_Gate
  and c1___t5___all (c1___t5___all_out, ~Clock, T5, or_2_out);  // AND_Gate
  or or_1 (or_1_out, c1___t5___all_out, c1___others_out);
  and nb4___others (D1, ~b4, or_1_out);  // AND_Gate
  or or_2 (or_2_out, _000_out, _011_out, _100_out, _110_out);
  and c1___others (c1___others_out, Clock, T6, or_2_out);
  and b4___others (D2, b4, or_1_out);
endmodule

// L R A S
module L__R__A__S (
  input  T2,
  input  T3,
  input  T4,
  input  T5,
  input  b7,
  input  b6,
  input  b5,
  input  b4,
  input  Clock,
  output A_S,
  output L,
  output R
);

  wire _000_out, _001_out, _010_out, _011_out, and_1_out, and_2_out, and_3_out, and_4_out, and_5_out,
       and_6_out, and_7_out, and_8_out, and_9_out, and_10_out, or_1_out;

  and _000 (_000_out, ~b7, ~b6, ~b5);  // AND_Gate
  and _001 (_001_out, ~b7, ~b6, b5);  // AND_Gate
  and _010 (_010_out, ~b7, b6, ~b5);  // AND_Gate
  and _011 (_011_out, ~b7, b6, b5);  // AND_Gate
  or or_1 (or_1_out, _000_out, _001_out, _010_out, _011_out);
  and and_1 (and_1_out, ~Clock, or_1_out, or_1_out, T2, ~b4);  // AND_Gate
  and and_2 (and_2_out, Clock, Clock, or_1_out, T3, ~b4);  // AND_Gate
  and and_3 (and_3_out, ~Clock, or_1_out, or_1_out, T3, ~b4);  // AND_Gate
  and and_4 (and_4_out, Clock, Clock, or_1_out, T4, ~b4);  // AND_Gate
  and and_5 (and_5_out, ~Clock, or_1_out, or_1_out, T2, b4);  // AND_Gate
  or or_2 (L, and_3_out, and_4_out, and_5_out, and_6_out);
  or or_3 (R, and_1_out, and_2_out, and_8_out, and_7_out);
  and and_6 (and_6_out, Clock, Clock, or_1_out, T3, b4);
  and and_7 (and_7_out, Clock, Clock, or_1_out, T4, b4);
  and and_8 (and_8_out, ~Clock, or_1_out, or_1_out, T3, b4);  // AND_Gate
  and and_9 (and_9_out, ~Clock, or_1_out, T4);  // AND_Gate
  or or_4 (A_S, and_9_out, and_10_out);
  and and_10 (and_10_out, Clock, or_1_out, T5);
endmodule

module PC (
  input  readFromBranch,
  input  T0,
  input  T5,
  input  T6,
  input  b7,
  input  b6,
  input  b5,
  input  Clock,
  output PC
);

  wire _001_or_010_out, _001_out, _010_out, and_1_out, c1___A___t6_2_out, c1___A___t6_out;

  and _010 (_010_out, ~b7, b6, ~b5);  // AND_Gate
  and _001 (_001_out, ~b7, ~b6, b5);  // AND_Gate
  or _001_or_010 (_001_or_010_out, _001_out, _010_out);
  and c1___A___t6 (c1___A___t6_out, readFromBranch, Clock, _001_or_010_out, T6);
  and c1___A___t6_2 (c1___A___t6_2_out, readFromBranch, ~Clock, T5, _001_or_010_out);  // AND_Gate
  or _001_or_010_2 (PC, c1___A___t6_out, and_1_out, c1___A___t6_2_out, T0);
  and and_1 (and_1_out, ~Clock, T6);  // AND_Gate
endmodule

module DISP (
  input  T5,
  input  T6,
  input  b7,
  input  b6,
  input  b5,
  input  Clock,
  output DISP
);

  wire c0___111___t5_out, c1___111___t6_out;

  and c1___111___t6 (c1___111___t6_out, Clock, b5, b6, b7, T6);
  or or_1 (DISP, c1___111___t6_out, c0___111___t5_out);
  and c0___111___t5 (c0___111___t5_out, ~Clock, b5, T5, b6, b7);  // AND_Gate
endmodule

module Mode (
  input  T4,
  input  T5,
  input  T6,
  input  b7,
  input  b6,
  input  b5,
  input  Clock,
  output Mode
);

  wire _101_out, t5_or__t6___c1_out, t6___c1_2_out, t6___c1_3_out, t6___c1_out;

  and _101 (_101_out, b7, ~b6, b5);  // AND_Gate
  and t6___c1 (t6___c1_out, ~Clock, T5);  // AND_Gate
  and t6___c1_2 (t6___c1_2_out, ~Clock, T4);  // AND_Gate
  or t5_or__t6___c1 (t5_or__t6___c1_out, t6___c1_2_out, t6___c1_out, t6___c1_3_out);
  and and_1 (Mode, _101_out, t5_or__t6___c1_out);
  and t6___c1_3 (t6___c1_3_out, Clock, T6);
endmodule

// ALUcontrol
module ALU210 (
  input  T6,
  input  T4,
  input  T5,
  input  b7,
  input  b6,
  input  b5,
  input  b3,
  input  Clock,
  output ALU2,
  output ALU0,
  output ALU1
);

  wire _000_out, _001_or_011_out, _001_out, _010___011_2_out, _010_out, _011_out,
       c1___000x_n0000____t3_4_5_6_2_out, c1___000x_n0000____t3_4_5_6_out, c1___001_011___t3_4_5_6_2_out,
       c1___001_011___t3_4_5_6_3_out, c1___001_011___t3_4_5_6_4_out, c1___001_011___t3_4_5_6_5_out,
       c1___001_011___t3_4_5_6_out, c1___010_011___t3_4_5_6_2_out, c1___010_011___t3_4_5_6_3_out,
       c1___010_011___t3_4_5_6_out;

  and _000 (_000_out, ~b7, ~b6, ~b5);  // AND_Gate
  and c1___000x_n0000____t3_4_5_6 (c1___000x_n0000____t3_4_5_6_out, ~Clock, b3, _000_out, T4);  // AND_Gate
  and _001 (_001_out, ~b7, ~b6, b5);  // AND_Gate
  and _010 (_010_out, ~b7, b6, ~b5);  // AND_Gate
  and c1___000x_n0000____t3_4_5_6_2 (c1___000x_n0000____t3_4_5_6_2_out, Clock, b3, _000_out, T5);
  or _010___011 (ALU2, c1___000x_n0000____t3_4_5_6_out, c1___000x_n0000____t3_4_5_6_2_out);
  and _011 (_011_out, ~b7, b6, b5);  // AND_Gate
  and c1___010_011___t3_4_5_6 (c1___010_011___t3_4_5_6_out, ~Clock, _010___011_2_out, T4);  // AND_Gate
  or _010___011_2 (_010___011_2_out, _010_out, _011_out);
  and c1___010_011___t3_4_5_6_2 (c1___010_011___t3_4_5_6_2_out, ~Clock, _010___011_2_out, T4);  // AND_Gate
  or _010___011_3 (ALU1, c1___010_011___t3_4_5_6_out, c1___010_011___t3_4_5_6_2_out, c1___010_011___t3_4_5_6_3_out, c1___001_011___t3_4_5_6_out);
  and c1___010_011___t3_4_5_6_3 (c1___010_011___t3_4_5_6_3_out, Clock, _010___011_2_out, T5);
  and c1___001_011___t3_4_5_6 (c1___001_011___t3_4_5_6_out, _010_out, Clock, T6);
  or _001_or_011 (_001_or_011_out, _001_out, _011_out);
  and c1___001_011___t3_4_5_6_2 (c1___001_011___t3_4_5_6_2_out, ~Clock, T4, _001_or_011_out);  // AND_Gate
  and c1___001_011___t3_4_5_6_3 (c1___001_011___t3_4_5_6_3_out, _001_or_011_out, T5);  // AND_Gate
  or _010___011_4 (ALU0, c1___001_011___t3_4_5_6_3_out, c1___001_011___t3_4_5_6_2_out, c1___001_011___t3_4_5_6_5_out, c1___001_011___t3_4_5_6_4_out);
  and c1___001_011___t3_4_5_6_4 (c1___001_011___t3_4_5_6_4_out, Clock, _001_or_011_out, T4);
  and c1___001_011___t3_4_5_6_5 (c1___001_011___t3_4_5_6_5_out, Clock, _001_out, T6);
endmodule

module Bus_Controls (
  input  T1,
  input  T2,
  input  T3,
  input  T4,
  input  T5,
  input  T6,
  input  b7,
  input  b6,
  input  b5,
  input  b3,
  input  b2,
  input  b1,
  input  b0,
  input  Clock,
  output [1:0] MUX_SBD_Select,
  output [1:0] DMX_SB_Select,
  output [1:0] DMX_CB_Select,
  output [1:0] MUX_CB_Select,
  output CB_Enabler
);

  wire _000_out, _001_out, _010_out, _011_out, _100_out, _101_out, _110_out, _111_out,
       add_beq_bnq_store_sub_mult_out, add_mult_sub_out, ADD_out, add_sub_beq_bnq_mult_out,
       add_sub_beq_bnq_mult_print_out, add_sub_load_inp_mult_out, and_1_out, and_2_out, and_3_out, and_4_out,
       and_5_out, and_6_out, and_7_out, and_8_out, and_9_out, and_10_out, and_11_out, and_12_out, and_13_out,
       and_14_out, and_15_out, and_16_out, and_17_out, and_18_out, and_19_out, and_20_out, and_21_out,
       and_22_out, and_23_out, and_24_out, and_25_out, and_26_out, mult_add_sub_bew_bnq_out, MULT_out,
       PRT_out, t2_lo_2_out, t2_lo_3_out, t2_lo_out, t3_hi_2_out, t3_hi_3_out, t3_hi_out, t3_lo_2_out,
       t3_lo_3_out, t3_lo_4_out, t3_lo_5_out, t3_lo_out, t4_hi_2_out, t4_hi_3_out, t4_hi_4_out, t4_hi_5_out,
       t4_hi_out, t5_lo_2_out, t5_lo_out, t6_hi_2_out, t6_hi_out;

  and _000 (_000_out, ~b7, ~b6, ~b5);  // AND_Gate
  and _001 (_001_out, ~b7, ~b6, b5);  // AND_Gate
  and _011 (_011_out, ~b7, b6, b5);  // AND_Gate
  and _010 (_010_out, ~b7, b6, ~b5);  // AND_Gate
  and _100 (_100_out, b7, ~b6, ~b5);  // AND_Gate
  and _101 (_101_out, b7, ~b6, b5);  // AND_Gate
  and and_1 (and_1_out, ~b0, ~b1, ~b2, ~b3);  // AND_Gate
  and MULT (MULT_out, _000_out, ~and_1_out);  // AND_Gate
  and _110 (_110_out, b7, b6, ~b5);  // AND_Gate
  and _111 (_111_out, b7, b6, b5);
  and PRT (PRT_out, _111_out, and_1_out);
  and ADD (ADD_out, _000_out, and_1_out);
  and and_2 (and_2_out, ~Clock, T1);  // AND_Gate
  and and_3 (and_3_out, Clock, T2);
  and and_4 (and_4_out, ~Clock, T4, _100_out);  // AND_Gate
  and and_5 (and_5_out, Clock, T5, _100_out);
  and and_6 (and_6_out, Clock, T5, _110_out);
  and and_7 (and_7_out, ~Clock, T4, _110_out);  // AND_Gate
  or or_1 (MUX_SBD_Select[1], and_2_out, and_3_out, and_4_out, and_5_out, and_7_out, and_6_out);
  and and_8 (and_8_out, Clock, T5, _101_out);
  and and_9 (and_9_out, ~Clock, T4, _101_out);  // AND_Gate
  and and_10 (and_10_out, ~Clock, T5, PRT_out);  // AND_Gate
  or or_2 (MUX_SBD_Select[0], and_7_out, and_6_out, and_9_out, and_8_out, and_10_out, and_11_out);
  and and_11 (and_11_out, Clock, T6, PRT_out);
  and and_12 (and_12_out, ~Clock, T4, _101_out);  // AND_Gate
  and and_13 (and_13_out, Clock, T5, _101_out);
  and and_14 (and_14_out, ~Clock, T5, PRT_out);  // AND_Gate
  and and_15 (and_15_out, Clock, T6, PRT_out);
  or or_3 (DMX_SB_Select[1], and_12_out, and_13_out, and_14_out, and_15_out);
  and and_16 (and_16_out, ~Clock, T1);  // AND_Gate
  and and_17 (and_17_out, Clock, T2);
  and and_18 (and_18_out, ~Clock, _100_out, T4);  // AND_Gate
  or or_4 (DMX_SB_Select[0], and_15_out, and_16_out, and_17_out, and_18_out, and_19_out, and_21_out, and_20_out, and_23_out, and_23_out);
  and and_19 (and_19_out, Clock, _100_out, T5);
  and and_20 (and_20_out, Clock, T5, _110_out);
  and and_21 (and_21_out, ~Clock, T4, _110_out);  // AND_Gate
  and and_22 (and_22_out, ~Clock, _100_out, T5);  // AND_Gate
  and and_23 (and_23_out, ~Clock, T5, PRT_out);  // AND_Gate
  and and_24 (and_24_out, ~Clock, T5, _110_out);  // AND_Gate
  and and_25 (and_25_out, Clock, _100_out, T6);
  and and_26 (and_26_out, Clock, T6, _110_out);
  or or_5 (CB_Enabler, and_22_out, and_25_out, and_24_out, and_26_out, MUX_CB_Select[1], MUX_CB_Select[0]);
  and t5_lo (t5_lo_out, ~Clock, add_mult_sub_out, T5);  // AND_Gate
  or add_mult_sub (add_mult_sub_out, ADD_out, MULT_out, _011_out);
  and t3_lo (t3_lo_out, ~Clock, MULT_out, T3);  // AND_Gate
  and t6_hi (t6_hi_out, Clock, add_mult_sub_out, T6);
  and t4_hi (t4_hi_out, Clock, MULT_out, T4);
  or bit_1 (MUX_CB_Select[1], t5_lo_out, t6_hi_out, t3_lo_out, t4_hi_out);
  or add_sub_beq_bnq_mult_print (add_sub_beq_bnq_mult_print_out, MULT_out, ADD_out, _001_out, _010_out, _011_out, PRT_out);
  and t2_lo (t2_lo_out, ~Clock, add_sub_beq_bnq_mult_print_out, T2);  // AND_Gate
  and t4_hi_2 (t4_hi_2_out, Clock, add_beq_bnq_store_sub_mult_out, T4);
  and t3_lo_2 (t3_lo_2_out, ~Clock, add_beq_bnq_store_sub_mult_out, T3);  // AND_Gate
  and t3_hi (t3_hi_out, Clock, add_sub_beq_bnq_mult_print_out, T3);
  or bit_0 (MUX_CB_Select[0], t2_lo_out, t3_hi_out, t3_lo_2_out, t4_hi_2_out);
  or add_beq_bnq_store_sub_mult (add_beq_bnq_store_sub_mult_out, ADD_out, _001_out, _010_out, _011_out, _101_out, MULT_out);
  or add_sub_load_inp_mult (add_sub_load_inp_mult_out, ADD_out, MULT_out, _011_out, _100_out, _110_out);
  and t6_hi_2 (t6_hi_2_out, Clock, add_sub_load_inp_mult_out, T6);
  and t5_lo_2 (t5_lo_2_out, ~Clock, add_sub_load_inp_mult_out, T5);  // AND_Gate
  and t3_hi_2 (t3_hi_2_out, Clock, T3, add_sub_beq_bnq_mult_out);
  and t2_lo_2 (t2_lo_2_out, ~Clock, T2, add_sub_beq_bnq_mult_out);  // AND_Gate
  or bit1 (DMX_CB_Select[1], t4_hi_4_out, t5_lo_2_out, t6_hi_2_out, t2_lo_2_out, t3_hi_2_out, t3_lo_3_out, t4_hi_3_out);
  or add_sub_beq_bnq_mult (add_sub_beq_bnq_mult_out, MULT_out, ADD_out, _001_out, _010_out, _011_out);
  and t4_hi_3 (t4_hi_3_out, Clock, add_sub_beq_bnq_mult_out, T5);
  and t3_lo_3 (t3_lo_3_out, ~Clock, add_sub_beq_bnq_mult_out, T3);  // AND_Gate
  or mult_add_sub_bew_bnq (mult_add_sub_bew_bnq_out, MULT_out, _001_out, _010_out, _011_out, ADD_out);
  and t3_lo_4 (t3_lo_4_out, ~Clock, T3, mult_add_sub_bew_bnq_out);  // AND_Gate
  and t3_lo_5 (t3_lo_5_out, ~Clock, T3, _101_out);  // AND_Gate
  and t4_hi_4 (t4_hi_4_out, Clock, T4, mult_add_sub_bew_bnq_out);
  and t2_lo_3 (t2_lo_3_out, ~Clock, PRT_out, T2);  // AND_Gate
  and t4_hi_5 (t4_hi_5_out, Clock, T4, _101_out);
  and t3_hi_3 (t3_hi_3_out, Clock, PRT_out, T3);
  or bit0 (DMX_CB_Select[0], t2_lo_2_out, t4_hi_5_out, t2_lo_3_out, t3_hi_3_out, t4_hi_4_out, t3_lo_4_out, t3_lo_5_out, t3_hi_2_out, t3_lo_3_out, t4_hi_3_out);

  // Notes on the sheet:
  //   DMX: demultplexer, MUX: multiplexer
  //   CB: CPU Bus, SBd: System Bus (Data)
  //   mbr 01
  //   D1/D1 10
  //   L/R 11
endmodule

// OM
module Other_MUX_Controls (
  input  T2,
  input  T3,
  input  T4,
  input  T5,
  input  T6,
  input  b7,
  input  b6,
  input  b5,
  input  b4,
  input  b3,
  input  b2,
  input  b1,
  input  b0,
  input  Clock,
  output MUX_MAR_Enabler,
  output R_L_Select,
  output MUX_MBR,
  output D1_D2_Select
);

  wire _000_out, _001_out, _010_out, _011_out, _100_out, _101_out, _110_out, _111_out,
       add__sub__beq__bneq__mult_out, ADD_out, add_sub_beq_bnq_out, add_sub_load_inp_mult_out, and_1_out,
       and_2_out, and_3_out, and_4_out, and_5_out, and_6_out, and_7_out, and_8_out, and_9_out, and_10_out,
       and_11_out, and_12_out, and_13_out, MULT_out, or_1_out, or_3_out, or_4_out, or_6_out, or_7_out,
       PRT_out, t2_lo_b4_all_out, t2_lo_t3_hi_out, t3_hi_b4_all_out, t3_lo__b4_out, t3_lo_b4_sub_out,
       t3_lo_t4_hi_out, t4_hi__b4_out, t4_hi_b4_store_out, t4_hi_b4_sub_out, t5_lo_b4_out, t6_hi_b4_out;

  and _000 (_000_out, ~b7, ~b6, ~b5);  // AND_Gate
  and _010 (_010_out, ~b7, b6, ~b5);  // AND_Gate
  and _001 (_001_out, ~b7, ~b6, b5);  // AND_Gate
  and _100 (_100_out, b7, ~b6, ~b5);  // AND_Gate
  and _011 (_011_out, ~b7, b6, b5);  // AND_Gate
  and and_1 (and_1_out, ~b0, ~b1, ~b2, ~b3);  // AND_Gate
  and _110 (_110_out, b7, b6, ~b5);  // AND_Gate
  and _101 (_101_out, b7, ~b6, b5);  // AND_Gate
  and MULT (MULT_out, _000_out, ~and_1_out);  // AND_Gate
  and and_2 (and_2_out, ~Clock, b4, _101_out, T3);  // AND_Gate
  and _111 (_111_out, b7, b6, b5);
  and PRT (PRT_out, _111_out, and_1_out);
  and ADD (ADD_out, _000_out, and_1_out);
  or or_1 (or_1_out, _101_out, _100_out);
  and and_3 (and_3_out, Clock, T3, or_1_out);
  or or_2 (MUX_MAR_Enabler, and_3_out, and_5_out);
  and and_4 (and_4_out, ~Clock, T2);  // AND_Gate
  or or_3 (or_3_out, _101_out, _100_out);
  and and_5 (and_5_out, T2, or_3_out);
  and and_6 (and_6_out, Clock, T3);
  or add__sub__beq__bneq__mult (add__sub__beq__bneq__mult_out, MULT_out, ADD_out, _011_out, _010_out, _001_out);
  or or_4 (or_4_out, and_4_out, and_6_out);
  and t2_lo_t3_hi (t2_lo_t3_hi_out, ~b4, or_4_out, add__sub__beq__bneq__mult_out);  // AND_Gate
  or or_5 (R_L_Select, t2_lo_t3_hi_out, t3_lo_t4_hi_out);
  and and_7 (and_7_out, ~Clock, T3);  // AND_Gate
  and and_8 (and_8_out, Clock, T4);
  or or_6 (or_6_out, and_7_out, and_8_out);
  and t3_hi_b4_all (t3_hi_b4_all_out, b4, Clock, T3, or_7_out);
  and t3_lo_t4_hi (t3_lo_t4_hi_out, add__sub__beq__bneq__mult_out, b4, or_6_out);
  or or_7 (or_7_out, MULT_out, ADD_out, PRT_out, _001_out, _010_out);
  and t4_hi_b4_store (t4_hi_b4_store_out, Clock, b4, _101_out, T4);
  and t2_lo_b4_all (t2_lo_b4_all_out, or_7_out, ~Clock, b4, T2);  // AND_Gate
  or or_8 (D1_D2_Select, and_2_out, and_2_out, t2_lo_b4_all_out, t3_hi_b4_all_out, t4_hi_b4_store_out, t4_hi__b4_out, t5_lo_b4_out, t6_hi_b4_out, t3_lo__b4_out, t3_lo_b4_sub_out, t4_hi_b4_sub_out);
  and t4_hi__b4 (t4_hi__b4_out, ~b4, Clock, T4, add_sub_beq_bnq_out);  // AND_Gate
  and t3_lo__b4 (t3_lo__b4_out, ~Clock, ~b4, T3, add_sub_beq_bnq_out);  // AND_Gate
  or add_sub_beq_bnq (add_sub_beq_bnq_out, ADD_out, _001_out, _010_out, _011_out);
  and t5_lo_b4 (t5_lo_b4_out, ~Clock, add_sub_load_inp_mult_out, b4, T5);  // AND_Gate
  or add_sub_load_inp_mult (add_sub_load_inp_mult_out, MULT_out, ADD_out, _011_out, _100_out, _110_out);
  and t6_hi_b4 (t6_hi_b4_out, Clock, T6, b4, add_sub_load_inp_mult_out);
  and t3_lo_b4_sub (t3_lo_b4_sub_out, T3, ~Clock, _011_out, b4);  // AND_Gate
  and and_9 (and_9_out, Clock, T4, _101_out);
  and t4_hi_b4_sub (t4_hi_b4_sub_out, b4, T4, Clock, _011_out);
  and and_10 (and_10_out, ~Clock, T3, _101_out);  // AND_Gate
  and and_11 (and_11_out, Clock, T3, PRT_out);
  or or_9 (MUX_MBR, and_9_out, and_11_out, and_12_out, and_10_out, and_13_out);
  and and_12 (and_12_out, ~Clock, T2, _111_out);  // AND_Gate
  and and_13 (and_13_out, ~Clock, T2, _101_out);  // AND_Gate

  // Notes on the sheet:
  //   L/R Select: Left or Right ALU Register: 0 is left, 1 is right
  //   D1/D2 Select: D1 or D2 general purpose registers: 0 is D1, 1 is D2
  //   MUX MAR: inputs address from PC when 0 or IR when 1 (beq or bnq)
endmodule

module BEQ_BNQ (
  input  ALUc1,
  input  ALUc0,
  input  t5,
  input  t6,
  input  clock,
  output BEQ_BNQ
);

  wire and_1_out, and_2_out, and_4_out, or_1_out, or_2_out;

  and and_1 (and_1_out, ~clock, t5);  // AND_Gate
  or or_1 (or_1_out, and_1_out, t6);
  and and_2 (and_2_out, ALUc1, ~ALUc0);  // AND_Gate
  and and_3 (BEQ_BNQ, or_1_out, or_2_out);
  and and_4 (and_4_out, ~ALUc1, ALUc0);  // AND_Gate
  or or_2 (or_2_out, and_2_out, and_4_out);
endmodule
