// Logisim project Display.circ as structural Verilog: 2 circuits, main circuit main
// DISPLAY
module main (
  input  Clock,
  input  Enabler,
  input  RESET,
  input  _7,
  input  _6,
  input  _5,
  input  _4,
  input  _3,
  input  _2,
  input  _1,
  input  _0,
  output _0a,
  output _2a,
  output _0b,
  output _2b,
  output _0c,
  output _2c,
  output _0d,
  output _2d,
  output _0e,
  output _2e,
  output _0f,
  output _2f,
  output _0g,
  output _2g,
  output _1a,
  output _1b,
  output _1c,
  output _1d,
  output _1e,
  output _1f,
  output _1g
);

  wire and_1_out, and_2_out, and_3_out, and_4_out, and_5_out, and_6_out, and_7_out, and_8_out, and_9_out,
       and_10_out, and_11_out, and_12_out, and_13_out, and_14_out, and_15_out, and_16_out, and_17_out,
       and_18_out, and_19_out, and_20_out, and_21_out, and_22_out, and_23_out, and_24_out, and_25_out,
       and_26_out, and_27_out, and_28_out, and_29_out, and_30_out, and_31_out, and_32_out, and_33_out,
       and_34_out, and_35_out, and_36_out, and_37_out, and_38_out, and_39_out, and_40_out, and_41_out,
       and_42_out, and_43_out, and_44_out, and_45_out, and_46_out, and_47_out, and_48_out, and_49_out,
       and_50_out, and_51_out, and_52_out, and_53_out, and_54_out, and_55_out, and_56_out, and_57_out,
       and_58_out, and_59_out, and_60_out, and_61_out, and_62_out, and_63_out, and_64_out, and_65_out,
       and_66_out, and_67_out, and_68_out, and_69_out, and_70_out, and_71_out, and_72_out, and_73_out,
       and_74_out, and_75_out, and_76_out, and_77_out, and_78_out, and_79_out, and_80_out, and_81_out,
       and_82_out, and_83_out, and_84_out, and_85_out, and_86_out, and_87_out, and_88_out, and_89_out,
       and_90_out, and_91_out, and_92_out, and_93_out, and_94_out, and_95_out, and_96_out, and_97_out,
       and_98_out, and_99_out, and_100_out, and_101_out, falling_8_bit_register_1_output_pin_0,
       falling_8_bit_register_1_output_pin_1, falling_8_bit_register_1_output_pin_2,
       falling_8_bit_register_1_output_pin_3, falling_8_bit_register_1_output_pin_4,
       falling_8_bit_register_1_output_pin_5, falling_8_bit_register_1_output_pin_6,
       falling_8_bit_register_1_output_pin_7, not_1_out, not_2_out, not_3_out, not_4_out, not_5_out,
       not_6_out, not_7_out, not_8_out, not_9_out, not_10_out, not_11_out, not_12_out, not_13_out,
       not_14_out, not_15_out, not_16_out, not_17_out, not_18_out, not_19_out, not_20_out, not_21_out,
       not_22_out, not_23_out, not_24_out, not_25_out, not_26_out, not_27_out, not_28_out, not_29_out,
       not_30_out, not_31_out, not_32_out, not_33_out, not_34_out, not_35_out, not_36_out, not_37_out,
       not_38_out, not_39_out, not_40_out, not_41_out, not_42_out, not_43_out, not_44_out, not_45_out,
       not_46_out, not_47_out, not_48_out, not_49_out, not_50_out, not_51_out, not_52_out, not_53_out,
       not_54_out, not_55_out, not_56_out, not_57_out, not_58_out, not_59_out, not_60_out, not_61_out,
       not_62_out, not_63_out, not_64_out, not_65_out, not_66_out, not_67_out, not_68_out, not_69_out,
       not_70_out, not_71_out, not_72_out, not_73_out, not_74_out, not_75_out, not_76_out, not_77_out,
       not_78_out, not_79_out, not_80_out, not_81_out, not_82_out, not_83_out, not_84_out, not_85_out,
       not_86_out, not_87_out, not_88_out, not_89_out, not_90_out, not_91_out, not_92_out, not_93_out,
       not_94_out, not_95_out, not_96_out, not_97_out, not_98_out, or_1_out, or_2_out, or_3_out, or_4_out,
       or_5_out, or_6_out, or_7_out, or_8_out, or_9_out, or_10_out, or_11_out, or_12_out, or_13_out,
       or_14_out, or_15_out, or_16_out, or_17_out, or_18_out, or_19_out, or_20_out, or_21_out, or_22_out,
       or_23_out, or_24_out, or_25_out, or_26_out, or_27_out, or_28_out, or_29_out, or_30_out, or_31_out,
       or_32_out, or_33_out, or_34_out, or_35_out, or_36_out, or_37_out, or_38_out, or_39_out, or_40_out,
       or_41_out, or_42_out, or_43_out, or_44_out, or_45_out, or_46_out, or_47_out, or_48_out, or_49_out,
       or_50_out, or_51_out, or_52_out, or_53_out, or_54_out, or_55_out, or_56_out, or_57_out, or_58_out,
       or_59_out, or_60_out, or_61_out, or_62_out, or_63_out, or_64_out, or_65_out, or_66_out, or_67_out,
       or_68_out, or_69_out, or_70_out, or_71_out, or_72_out, or_73_out, or_74_out, or_75_out, or_76_out,
       or_77_out, or_78_out, or_79_out, or_80_out, or_81_out, or_82_out, or_83_out, or_84_out, or_85_out,
       or_86_out, or_87_out, or_88_out, or_89_out, or_90_out, or_91_out, or_92_out, or_93_out, xor_1_out,
       xor_2_out, xor_3_out, xor_4_out, xor_5_out, xor_6_out, xor_7_out, xor_8_out, xor_9_out, xor_10_out,
       xor_11_out, xor_12_out, xor_13_out, xor_14_out, xor_15_out, xor_16_out, xor_17_out, xor_18_out,
       xor_19_out, xor_20_out, xor_21_out;

  and and_1 (and_1_out, not_1_out, falling_8_bit_register_1_output_pin_0);
  not not_1 (not_1_out, falling_8_bit_register_1_output_pin_0);
  xor xor_1 (xor_1_out, and_1_out, falling_8_bit_register_1_output_pin_0);
  or or_1 (or_1_out, falling_8_bit_register_1_output_pin_2, falling_8_bit_register_1_output_pin_1);
  or or_2 (or_2_out, falling_8_bit_register_1_output_pin_1, falling_8_bit_register_1_output_pin_2);
  and and_2 (and_2_out, xor_1_out, or_1_out);
  not not_2 (not_2_out, or_2_out);
  and and_3 (and_3_out, falling_8_bit_register_1_output_pin_0, or_3_out);
  or or_3 (or_3_out, falling_8_bit_register_1_output_pin_1, falling_8_bit_register_1_output_pin_2);
  Falling_8_bit_Register falling_8_bit_register_1 (
    .Input_Pin_0(_7), .Input_Pin_1(_6), .Input_Pin_2(_5), .Input_Pin_3(_4), .Input_Pin_4(_3),
    .Input_Pin_5(_2), .Input_Pin_6(_1), .Input_Pin_7(_0),
    .Output_Pin_0(falling_8_bit_register_1_output_pin_0),
    .Output_Pin_1(falling_8_bit_register_1_output_pin_1),
    .Output_Pin_2(falling_8_bit_register_1_output_pin_2),
    .Output_Pin_3(falling_8_bit_register_1_output_pin_3),
    .Output_Pin_4(falling_8_bit_register_1_output_pin_4),
    .Output_Pin_5(falling_8_bit_register_1_output_pin_5),
    .Output_Pin_6(falling_8_bit_register_1_output_pin_6),
    .Output_Pin_7(falling_8_bit_register_1_output_pin_7), .Enabler(Enabler), .Clock(Clock), .RESET(RESET));
  or or_4 (or_4_out, and_1_out, and_3_out);
  or or_5 (or_5_out, falling_8_bit_register_1_output_pin_1, falling_8_bit_register_1_output_pin_2);
  and and_4 (and_4_out, or_4_out, not_3_out);
  not not_3 (not_3_out, falling_8_bit_register_1_output_pin_2);
  and and_5 (and_5_out, not_2_out, and_1_out);
  not not_4 (not_4_out, or_4_out);
  xor xor_2 (xor_2_out, or_5_out, falling_8_bit_register_1_output_pin_0);
  not not_5 (not_5_out, xor_3_out);
  xor xor_3 (xor_3_out, falling_8_bit_register_1_output_pin_1, falling_8_bit_register_1_output_pin_2);
  and and_6 (and_6_out, and_1_out, not_4_out);
  and and_7 (and_7_out, and_1_out, xor_2_out);
  and and_8 (and_8_out, not_4_out, falling_8_bit_register_1_output_pin_0);
  and and_9 (and_9_out, not_4_out, falling_8_bit_register_1_output_pin_1);
  and and_10 (and_10_out, not_5_out, or_4_out);
  and and_11 (and_11_out, falling_8_bit_register_1_output_pin_2, not_4_out);
  or or_6 (or_6_out, and_2_out, and_5_out, and_6_out);
  or or_7 (or_7_out, and_7_out, and_8_out);
  or or_8 (or_8_out, and_9_out, and_10_out);
  or or_9 (or_9_out, and_11_out, and_4_out);
  xor xor_4 (xor_4_out, or_7_out, or_8_out);
  or or_10 (or_10_out, falling_8_bit_register_1_output_pin_3, or_9_out);
  or or_11 (or_11_out, or_9_out, falling_8_bit_register_1_output_pin_3);
  _7_Segment_Display u_7_segment_display_1 (.g(_2g), .f(_2f), .a(_2a), .b(_2b), .e(_2e), .d(_2d), .c(_2c));  // open: dp
  and and_12 (and_12_out, xor_4_out, or_10_out);
  not not_6 (not_6_out, or_11_out);
  or or_12 (or_12_out, or_7_out, and_13_out);
  and and_13 (and_13_out, or_8_out, or_13_out);
  or or_13 (or_13_out, or_9_out, falling_8_bit_register_1_output_pin_3);
  _7_Segment_Display u_7_segment_display_2 (.g(_1g), .f(_1f), .a(_1a), .b(_1b), .e(_1e), .d(_1d), .c(_1c));  // open: dp
  not not_7 (not_7_out, or_12_out);
  or or_14 (or_14_out, or_9_out, falling_8_bit_register_1_output_pin_3);
  and and_14 (and_14_out, or_12_out, not_8_out);
  not not_8 (not_8_out, falling_8_bit_register_1_output_pin_3);
  and and_15 (and_15_out, not_6_out, or_7_out);
  xor xor_5 (xor_5_out, or_14_out, or_8_out);
  xor xor_6 (xor_6_out, or_9_out, falling_8_bit_register_1_output_pin_3);
  not not_9 (not_9_out, xor_6_out);
  _7_Segment_Display u_7_segment_display_3 (.g(_0g), .f(_0f), .a(_0a), .b(_0b), .e(_0e), .d(_0d), .c(_0c));  // open: dp
  and and_16 (and_16_out, or_7_out, not_7_out);
  and and_17 (and_17_out, or_7_out, xor_5_out);
  and and_18 (and_18_out, not_7_out, or_8_out);
  and and_19 (and_19_out, not_7_out, or_9_out);
  and and_20 (and_20_out, not_9_out, or_12_out);
  and and_21 (and_21_out, falling_8_bit_register_1_output_pin_3, not_7_out);
  or or_15 (or_15_out, and_12_out, and_15_out, and_16_out);
  or or_16 (or_16_out, and_17_out, and_18_out);
  or or_17 (or_17_out, and_19_out, and_20_out);
  or or_18 (or_18_out, and_21_out, and_14_out);
  xor xor_7 (xor_7_out, or_16_out, or_17_out);
  or or_19 (or_19_out, falling_8_bit_register_1_output_pin_4, or_18_out);
  or or_20 (or_20_out, or_18_out, falling_8_bit_register_1_output_pin_4);
  not not_10 (not_10_out, or_20_out);
  or or_21 (or_21_out, or_18_out, falling_8_bit_register_1_output_pin_4);
  and and_22 (and_22_out, xor_7_out, or_19_out);
  or or_22 (or_22_out, or_16_out, and_23_out);
  and and_23 (and_23_out, or_17_out, or_21_out);
  not not_11 (not_11_out, or_22_out);
  or or_23 (or_23_out, or_18_out, falling_8_bit_register_1_output_pin_4);
  xor xor_8 (xor_8_out, or_18_out, falling_8_bit_register_1_output_pin_4);
  not not_12 (not_12_out, falling_8_bit_register_1_output_pin_4);
  and and_24 (and_24_out, or_22_out, not_12_out);
  and and_25 (and_25_out, not_10_out, or_16_out);
  and and_26 (and_26_out, or_16_out, not_11_out);
  xor xor_9 (xor_9_out, or_23_out, or_17_out);
  not not_13 (not_13_out, xor_8_out);
  and and_27 (and_27_out, or_16_out, xor_9_out);
  and and_28 (and_28_out, not_11_out, or_17_out);
  and and_29 (and_29_out, not_11_out, or_18_out);
  and and_30 (and_30_out, not_13_out, or_22_out);
  and and_31 (and_31_out, falling_8_bit_register_1_output_pin_4, not_11_out);
  or or_24 (or_24_out, and_22_out, and_25_out, and_26_out);
  or or_25 (or_25_out, and_27_out, and_28_out);
  or or_26 (or_26_out, and_29_out, and_30_out);
  or or_27 (or_27_out, and_31_out, and_24_out);
  xor xor_10 (xor_10_out, and_1_out, or_6_out);
  and and_32 (and_32_out, xor_10_out, or_28_out);
  or or_28 (or_28_out, or_24_out, or_15_out);
  or or_29 (or_29_out, or_15_out, or_24_out);
  not not_14 (not_14_out, or_29_out);
  and and_33 (and_33_out, or_6_out, or_30_out);
  or or_30 (or_30_out, or_15_out, or_24_out);
  xor xor_11 (xor_11_out, or_25_out, or_26_out);
  and and_34 (and_34_out, xor_11_out, or_31_out);
  or or_31 (or_31_out, falling_8_bit_register_1_output_pin_5, or_27_out);
  not not_15 (not_15_out, or_32_out);
  or or_32 (or_32_out, or_27_out, falling_8_bit_register_1_output_pin_5);
  and and_35 (and_35_out, or_26_out, or_33_out);
  or or_33 (or_33_out, or_27_out, falling_8_bit_register_1_output_pin_5);
  or or_34 (or_34_out, and_1_out, and_33_out);
  not not_16 (not_16_out, or_24_out);
  or or_35 (or_35_out, or_25_out, and_35_out);
  not not_17 (not_17_out, falling_8_bit_register_1_output_pin_5);
  not not_18 (not_18_out, or_34_out);
  or or_36 (or_36_out, or_15_out, or_24_out);
  xor xor_12 (xor_12_out, or_15_out, or_24_out);
  and and_36 (and_36_out, or_34_out, not_16_out);
  not not_19 (not_19_out, or_35_out);
  or or_37 (or_37_out, or_27_out, falling_8_bit_register_1_output_pin_5);
  xor xor_13 (xor_13_out, or_27_out, falling_8_bit_register_1_output_pin_5);
  and and_37 (and_37_out, or_35_out, not_17_out);
  and and_38 (and_38_out, not_14_out, and_1_out);
  and and_39 (and_39_out, and_1_out, not_18_out);
  xor xor_14 (xor_14_out, or_36_out, or_6_out);
  not not_20 (not_20_out, xor_12_out);
  and and_40 (and_40_out, not_20_out, or_34_out);
  and and_41 (and_41_out, not_15_out, or_25_out);
  and and_42 (and_42_out, or_25_out, not_19_out);
  xor xor_15 (xor_15_out, or_37_out, or_26_out);
  not not_21 (not_21_out, xor_13_out);
  and and_43 (and_43_out, not_21_out, or_35_out);
  and and_44 (and_44_out, and_1_out, xor_14_out);
  and and_45 (and_45_out, not_18_out, or_6_out);
  and and_46 (and_46_out, not_18_out, or_15_out);
  and and_47 (and_47_out, or_24_out, not_18_out);
  and and_48 (and_48_out, or_25_out, xor_15_out);
  and and_49 (and_49_out, not_19_out, or_26_out);
  and and_50 (and_50_out, not_19_out, or_27_out);
  and and_51 (and_51_out, falling_8_bit_register_1_output_pin_5, not_19_out);
  or or_38 (or_38_out, and_32_out, and_38_out, and_39_out);
  or or_39 (or_39_out, and_44_out, and_45_out);
  or or_40 (or_40_out, and_46_out, and_40_out);
  or or_41 (or_41_out, and_47_out, and_36_out);
  or or_42 (or_42_out, and_34_out, and_41_out, and_42_out);
  or or_43 (or_43_out, and_48_out, and_49_out);
  or or_44 (or_44_out, and_50_out, and_43_out);
  or or_45 (or_45_out, and_51_out, and_37_out);
  xor xor_16 (xor_16_out, or_39_out, or_40_out);
  and and_52 (and_52_out, xor_16_out, or_46_out);
  or or_46 (or_46_out, or_42_out, or_41_out);
  not not_22 (not_22_out, or_47_out);
  or or_47 (or_47_out, or_41_out, or_42_out);
  and and_53 (and_53_out, or_40_out, or_48_out);
  or or_48 (or_48_out, or_41_out, or_42_out);
  xor xor_17 (xor_17_out, or_43_out, or_44_out);
  and and_54 (and_54_out, xor_17_out, or_49_out);
  or or_49 (or_49_out, falling_8_bit_register_1_output_pin_6, or_45_out);
  not not_23 (not_23_out, or_50_out);
  or or_50 (or_50_out, or_45_out, falling_8_bit_register_1_output_pin_6);
  and and_55 (and_55_out, or_44_out, or_51_out);
  or or_51 (or_51_out, or_45_out, falling_8_bit_register_1_output_pin_6);
  or or_52 (or_52_out, or_39_out, and_53_out);
  or or_53 (or_53_out, or_41_out, or_42_out);
  not not_24 (not_24_out, or_42_out);
  or or_54 (or_54_out, or_43_out, and_55_out);
  or or_55 (or_55_out, or_45_out, falling_8_bit_register_1_output_pin_6);
  not not_25 (not_25_out, falling_8_bit_register_1_output_pin_6);
  not not_26 (not_26_out, or_52_out);
  xor xor_18 (xor_18_out, or_53_out, or_40_out);
  xor xor_19 (xor_19_out, or_41_out, or_42_out);
  and and_56 (and_56_out, or_52_out, not_24_out);
  not not_27 (not_27_out, or_54_out);
  xor xor_20 (xor_20_out, or_55_out, or_44_out);
  xor xor_21 (xor_21_out, or_45_out, falling_8_bit_register_1_output_pin_6);
  and and_57 (and_57_out, or_54_out, not_25_out);
  and and_58 (and_58_out, not_22_out, or_39_out);
  and and_59 (and_59_out, or_39_out, not_26_out);
  and and_60 (and_60_out, not_26_out, or_40_out);
  and and_61 (and_61_out, not_26_out, or_41_out);
  not not_28 (not_28_out, xor_19_out);
  and and_62 (and_62_out, not_28_out, or_52_out);
  and and_63 (and_63_out, or_42_out, not_26_out);
  and and_64 (and_64_out, not_23_out, or_43_out);
  and and_65 (and_65_out, or_43_out, not_27_out);
  and and_66 (and_66_out, not_27_out, or_44_out);
  and and_67 (and_67_out, not_27_out, or_45_out);
  not not_29 (not_29_out, xor_21_out);
  and and_68 (and_68_out, not_29_out, or_54_out);
  and and_69 (and_69_out, falling_8_bit_register_1_output_pin_6, not_27_out);
  and and_70 (and_70_out, or_39_out, xor_18_out);
  and and_71 (and_71_out, or_43_out, xor_20_out);
  or or_56 (or_56_out, and_52_out, and_58_out, and_59_out);
  or or_57 (or_57_out, and_70_out, and_60_out);
  or or_58 (or_58_out, and_61_out, and_62_out);
  or or_59 (or_59_out, and_63_out, and_56_out);
  or or_60 (or_60_out, and_54_out, and_64_out, and_65_out);
  or or_61 (or_61_out, and_71_out, and_66_out);
  or or_62 (or_62_out, and_67_out, and_68_out);
  or or_63 (or_63_out, and_69_out, and_57_out);
  not not_30 (not_30_out, and_1_out);
  not not_31 (not_31_out, and_1_out);
  not not_32 (not_32_out, or_38_out);
  not not_33 (not_33_out, or_56_out);
  not not_34 (not_34_out, or_57_out);
  not not_35 (not_35_out, or_58_out);
  not not_36 (not_36_out, or_59_out);
  not not_37 (not_37_out, or_60_out);
  not not_38 (not_38_out, or_64_out);
  or or_64 (or_64_out, not_30_out, not_39_out);
  not not_39 (not_39_out, or_65_out);
  or or_65 (or_65_out, not_38_out, and_1_out);
  or or_66 (or_66_out, not_31_out, not_41_out);
  not not_40 (not_40_out, or_66_out);
  not not_41 (not_41_out, or_67_out);
  or or_67 (or_67_out, not_40_out, and_1_out);
  or or_68 (or_68_out, not_32_out, not_43_out);
  not not_42 (not_42_out, or_68_out);
  not not_43 (not_43_out, or_69_out);
  or or_69 (or_69_out, not_42_out, or_38_out);
  not not_44 (not_44_out, or_70_out);
  or or_70 (or_70_out, not_33_out, not_45_out);
  or or_71 (or_71_out, not_44_out, or_56_out);
  not not_45 (not_45_out, or_71_out);
  or or_72 (or_72_out, not_34_out, not_47_out);
  not not_46 (not_46_out, or_72_out);
  not not_47 (not_47_out, or_73_out);
  or or_73 (or_73_out, not_46_out, or_57_out);
  or or_74 (or_74_out, not_35_out, not_49_out);
  not not_48 (not_48_out, or_74_out);
  or or_75 (or_75_out, not_48_out, or_58_out);
  not not_49 (not_49_out, or_75_out);
  not not_50 (not_50_out, or_76_out);
  or or_76 (or_76_out, not_36_out, not_51_out);
  or or_77 (or_77_out, not_50_out, or_59_out);
  not not_51 (not_51_out, or_77_out);
  not not_52 (not_52_out, or_78_out);
  or or_78 (or_78_out, not_37_out, not_53_out);
  not not_53 (not_53_out, or_79_out);
  or or_79 (or_79_out, not_52_out, or_60_out);
  not not_54 (not_54_out, or_61_out);
  not not_55 (not_55_out, or_62_out);
  not not_56 (not_56_out, or_63_out);
  not not_57 (not_57_out, falling_8_bit_register_1_output_pin_7);
  or or_80 (or_80_out, not_54_out, not_59_out);
  not not_58 (not_58_out, or_80_out);
  or or_81 (or_81_out, not_58_out, or_61_out);
  not not_59 (not_59_out, or_81_out);
  not not_60 (not_60_out, or_82_out);
  or or_82 (or_82_out, not_55_out, not_61_out);
  not not_61 (not_61_out, or_83_out);
  or or_83 (or_83_out, not_60_out, or_62_out);
  or or_84 (or_84_out, not_56_out, not_63_out);
  not not_62 (not_62_out, or_84_out);
  not not_63 (not_63_out, or_85_out);
  or or_85 (or_85_out, not_62_out, or_63_out);
  or or_86 (or_86_out, not_57_out, not_65_out);
  not not_64 (not_64_out, or_86_out);
  not not_65 (not_65_out, or_87_out);
  or or_87 (or_87_out, not_64_out, falling_8_bit_register_1_output_pin_7);
  and and_72 (and_72_out, not_40_out, not_42_out, not_45_out);
  and and_73 (and_73_out, not_40_out, not_44_out, not_43_out);
  and and_74 (and_74_out, not_40_out, not_43_out, not_45_out);
  and and_75 (and_75_out, not_41_out, not_42_out, not_45_out);
  and and_76 (and_76_out, not_44_out, not_43_out, not_41_out);
  buf or_88 (or_88_out, not_72_out);  // OR_Gate
  or or_89 (or_89_out, not_39_out, and_77_out);
  and and_77 (and_77_out, not_41_out, not_43_out);
  and and_78 (and_78_out, not_44_out, not_39_out, not_41_out, not_43_out);
  and and_79 (and_79_out, not_42_out, not_41_out);
  and and_80 (and_80_out, not_44_out, not_42_out, not_40_out);
  and and_81 (and_81_out, not_45_out, not_43_out, not_41_out, not_39_out);
  and and_82 (and_82_out, not_48_out, not_50_out, not_53_out);
  and and_83 (and_83_out, not_48_out, not_52_out, not_51_out);
  and and_84 (and_84_out, not_48_out, not_51_out, not_53_out);
  and and_85 (and_85_out, not_49_out, not_50_out, not_53_out);
  and and_86 (and_86_out, not_52_out, not_51_out, not_49_out);
  buf or_90 (or_90_out, not_83_out);  // OR_Gate
  or or_91 (or_91_out, not_47_out, and_87_out);
  and and_87 (and_87_out, not_49_out, not_51_out);
  and and_88 (and_88_out, not_52_out, not_47_out, not_49_out, not_51_out);
  and and_89 (and_89_out, not_50_out, not_49_out);
  and and_90 (and_90_out, not_52_out, not_50_out, not_48_out);
  and and_91 (and_91_out, not_53_out, not_51_out, not_49_out, not_47_out);
  not not_66 (not_66_out, and_72_out);
  not not_67 (not_67_out, and_73_out);
  not not_68 (not_68_out, and_74_out);
  not not_69 (not_69_out, and_75_out);
  not not_70 (not_70_out, and_76_out);
  not not_71 (not_71_out, or_88_out);
  not not_72 (not_72_out, or_89_out);
  not not_73 (not_73_out, and_78_out);
  not not_74 (not_74_out, and_79_out);
  not not_75 (not_75_out, and_80_out);
  not not_76 (not_76_out, and_81_out);
  not not_77 (not_77_out, and_82_out);
  not not_78 (not_78_out, and_83_out);
  not not_79 (not_79_out, and_84_out);
  not not_80 (not_80_out, and_85_out);
  not not_81 (not_81_out, and_86_out);
  not not_82 (not_82_out, or_90_out);
  not not_83 (not_83_out, or_91_out);
  not not_84 (not_84_out, and_88_out);
  not not_85 (not_85_out, and_89_out);
  not not_86 (not_86_out, and_90_out);
  not not_87 (not_87_out, and_91_out);
  and and_92 (and_92_out, not_60_out, not_62_out, not_65_out);
  and and_93 (and_93_out, not_60_out, not_64_out, not_63_out);
  and and_94 (and_94_out, not_60_out, not_63_out, not_65_out);
  and and_95 (and_95_out, not_61_out, not_62_out, not_65_out);
  and and_96 (and_96_out, not_64_out, not_63_out, not_61_out);
  buf or_92 (or_92_out, not_94_out);  // OR_Gate
  or or_93 (or_93_out, not_59_out, and_97_out);
  and and_97 (and_97_out, not_61_out, not_63_out);
  and and_98 (and_98_out, not_64_out, not_59_out, not_61_out, not_63_out);
  and and_99 (and_99_out, not_62_out, not_61_out);
  and and_100 (and_100_out, not_64_out, not_62_out, not_60_out);
  and and_101 (and_101_out, not_65_out, not_63_out, not_61_out, not_59_out);
  not not_88 (not_88_out, and_92_out);
  not not_89 (not_89_out, and_93_out);
  not not_90 (not_90_out, and_94_out);
  not not_91 (not_91_out, and_95_out);
  not not_92 (not_92_out, and_96_out);
  not not_93 (not_93_out, or_92_out);
  not not_94 (not_94_out, or_93_out);
  not not_95 (not_95_out, and_98_out);
  not not_96 (not_96_out, and_99_out);
  not not_97 (not_97_out, and_100_out);
  not not_98 (not_98_out, and_101_out);
  and and_102 (_2a, not_68_out, not_66_out, not_71_out, not_73_out);
  and and_103 (_2b, not_66_out, not_67_out, not_71_out);
  and and_104 (_2c, not_69_out, not_71_out);
  and and_105 (_2d, not_70_out, not_68_out, not_75_out, not_71_out);
  and and_106 (_2e, not_71_out, not_68_out, not_45_out);
  and and_107 (_2f, not_73_out, not_71_out, not_75_out, not_74_out);
  and and_108 (_2g, not_73_out, not_71_out, not_75_out, not_76_out);
  and and_109 (_1a, not_79_out, not_77_out, not_82_out, not_84_out);
  and and_110 (_1b, not_77_out, not_78_out, not_82_out);
  and and_111 (_1c, not_80_out, not_82_out);
  and and_112 (_1d, not_81_out, not_79_out, not_86_out, not_82_out);
  and and_113 (_1e, not_82_out, not_79_out, not_53_out);
  and and_114 (_1f, not_84_out, not_82_out, not_86_out, not_85_out);
  and and_115 (_1g, not_84_out, not_82_out, not_86_out, not_87_out);
  and and_116 (_0a, not_90_out, not_88_out, not_93_out, not_95_out);
  and and_117 (_0b, not_88_out, not_89_out, not_93_out);
  and and_118 (_0c, not_91_out, not_93_out);
  and and_119 (_0d, not_92_out, not_90_out, not_97_out, not_93_out);
  and and_120 (_0e, not_93_out, not_90_out, not_65_out);
  and and_121 (_0f, not_95_out, not_93_out, not_97_out, not_96_out);
  and and_122 (_0g, not_95_out, not_93_out, not_97_out, not_98_out);

  // Notes on the sheet:
  //   Binary input in decreasing order of significance
  //   Decimal display in decreasing order of significance
endmodule

module test (
  input  in_1,
  input  in_2
);

  wire main_1__0a, main_1__0b, main_1__0c, main_1__0d, main_1__0e, main_1__0f, main_1__0g, main_1__1a,
       main_1__1b, main_1__1c, main_1__2a, main_1__2b, main_1__2c, main_1__2d, main_1__2e;

  _7_Segment_Display u_7_segment_display_1 (
    .g(main_1__2e), .f(main_1__2e), .a(main_1__2a), .b(main_1__2b), .e(main_1__2e), .d(main_1__2d),
    .c(main_1__2c));  // open: dp
  _7_Segment_Display u_7_segment_display_2 (
    .g(main_1__1c), .f(main_1__1a), .a(main_1__1a), .b(main_1__1b), .e(main_1__1c), .d(main_1__1c),
    .c(main_1__1c));  // open: dp
  main main_1 (
    ._2a(main_1__2a), ._2b(main_1__2b), ._2c(main_1__2c), ._2d(main_1__2d), ._2e(main_1__2e),
    ._2f(main_1__2e), ._2g(main_1__2e), ._0a(main_1__0a), ._0b(main_1__0b), ._0c(main_1__0c),
    ._0d(main_1__0d), ._0e(main_1__0e), ._0f(main_1__0f), ._0g(main_1__0g), ._1a(main_1__1a),
    ._1b(main_1__1b), ._1c(main_1__1c), ._1d(main_1__1c), ._1e(main_1__1c), ._1f(main_1__1a),
    ._1g(main_1__1c), .Clock(in_1), .Enabler(in_2), ._7(in_2), ._6(in_2), ._5(in_2), ._4(in_2), ._3(in_2),
    ._2(in_2), ._1(in_2));  // open: _0, RESET
  _7_Segment_Display u_7_segment_display_3 (
    .g(main_1__0g), .f(main_1__0f), .a(main_1__0a), .b(main_1__0b), .e(main_1__0e), .d(main_1__0d),
    .c(main_1__0c));  // open: dp
endmodule
