// Logisim project KeyBuffer.circ as structural Verilog: 1 circuit, main circuit main
// KEYPAD
module main (
  input  RESET,
  input  _0,
  input  _1,
  input  _2,
  input  _3,
  input  _4,
  input  _5,
  input  _6,
  input  _7,
  input  _8,
  input  _9,
  output _7_2,
  output _6_2,
  output _5_2,
  output _4_2,
  output _3_2,
  output _2_2,
  output _1_2,
  output _0_2
);

  wire or_1_out, or_2_out, or_3_out, or_4_out, or_5_out, or_6_out, or_7_out, or_8_out;

  or or_1 (or_1_out, _2, _7, _0, _1, RESET, _3, _4, _5, _6);
  D_Flip_Flop d_ff_1 (.Q(_7_2));  // open: clk, D, Qn, preset, en, reset
  or or_2 (or_2_out, _2, _0, _1, RESET, _3, _8, _9);
  D_Flip_Flop d_ff_2 (.Q(_6_2));  // open: clk, D, Qn, preset, en, reset
  or or_3 (or_3_out, _4, _0, _1, RESET, _5, _8, _9);
  or or_4 (or_4_out, _0, _2, _4, _6, _8, RESET);
  D_Flip_Flop d_ff_3 (.Q(_5_2));  // open: clk, D, Qn, preset, en, reset
  or or_5 (or_5_out, _9, _8);
  D_Flip_Flop d_ff_4 (.Q(_4_2));  // open: clk, D, Qn, preset, en, reset
  or or_6 (or_6_out, _7, _6, _5, _4);
  D_Flip_Flop d_ff_5 (.Q(_3_2), .preset(or_5_out), .reset(or_1_out));  // open: clk, D, Qn, en
  D_Flip_Flop d_ff_6 (.Q(_2_2), .preset(or_6_out), .reset(or_2_out));  // open: clk, D, Qn, en
  or or_7 (or_7_out, _7, _6, _3, _2);
  D_Flip_Flop d_ff_7 (.Q(_1_2), .preset(or_7_out), .reset(or_3_out));  // open: clk, D, Qn, en
  or or_8 (or_8_out, _9, _7, _5, _3, _1);
  D_Flip_Flop d_ff_8 (.Q(_0_2), .preset(or_8_out), .reset(or_4_out));  // open: clk, D, Qn, en

  // Notes on the sheet:
  //   Most significant
  //   Least significant
endmodule
