// Logisim project ProgramCounter.circ as structural Verilog: 1 circuit, main circuit Program Counter
// PC+INC
module Program_Counter (
  input  Enabler,
  input  Clock,
  input  Zero,
  input  [3:0] addresFromBranch,
  input  BEQ_or_BNQ,
  input  readFromBranch,
  output toMAR0,
  output toMAR1,
  output toMAR2,
  output toMAR3
);

  wire and_1_out;
  wire [3:0] adder_1_out, INC_output_pin_0, multiplexer_1_out;

  Multiplexer #(.width(4), .enable("false")) multiplexer_1 (
    .in0(adder_1_out), .in1(addresFromBranch), .out(multiplexer_1_out), .sel(and_1_out));
  and and_1 (and_1_out, BEQ_or_BNQ, readFromBranch);
  Falling_4_Bit_Register INC (
    .Input_Pin_0(multiplexer_1_out[0]), .Input_Pin_1(multiplexer_1_out[1]),
    .Input_Pin_2(multiplexer_1_out[2]), .Input_Pin_3(multiplexer_1_out[3]),
    .Output_Pin_0(INC_output_pin_0[0]), .Output_Pin_1(INC_output_pin_0[1]),
    .Output_Pin_2(INC_output_pin_0[2]), .Output_Pin_3(INC_output_pin_0[3]), .Enabler(Enabler), .Clock(Clock),
    .RESET(Zero));
  Falling_4_Bit_Register PC (
    .Input_Pin_0(INC_output_pin_0[0]), .Input_Pin_1(INC_output_pin_0[1]), .Input_Pin_2(INC_output_pin_0[2]),
    .Input_Pin_3(INC_output_pin_0[3]), .Output_Pin_0(toMAR0), .Output_Pin_1(toMAR1), .Output_Pin_2(toMAR2),
    .Output_Pin_3(toMAR3), .Enabler(Enabler), .Clock(Clock), .RESET(Zero));
  Adder #(.width(4)) adder_1 (.a(INC_output_pin_0), .b(4'b0001), .out(adder_1_out));  // open: cin, cout

  // Notes on the sheet:
  //   BEQ and BNQ: controlled by ALU c1 bit coming from ALU
  //   readFromBranch activated when status register from ALU is 1
endmodule
