// Logisim project RAM.circ as structural Verilog: 5 circuits, main circuit 16 Byte Memory
module RAM (
  input  R_W,
  input  Clock,
  input  MAR_0,
  input  MAR_1,
  input  MAR_2,
  input  MAR_3,
  input  RESET,
  input  From_MBR_0,
  input  From_MBR_1,
  input  From_MBR_2,
  input  From_MBR_3,
  input  From_MBR_4,
  input  From_MBR_5,
  input  From_MBR_6,
  input  CU_Enabler,
  input  From_MBR_7,
  output To_MBR_7,
  output To_MBR6,
  output To_MBR5,
  output To_MBR4,
  output To_MBR3,
  output To_MBR2,
  output To_MBR1,
  output To_MBR0
);

  wire and_1_out, and_2_out, and_3_out, and_4_out, and_5_out, and_6_out, and_7_out, and_8_out,
       decoder_1_out0, decoder_1_out1, decoder_1_out2, decoder_1_out3, decoder_1_out4, decoder_1_out5,
       decoder_1_out6, decoder_1_out7, decoder_1_out8, decoder_1_out9, decoder_1_out10, decoder_1_out11,
       decoder_1_out12, decoder_1_out13, decoder_1_out14, decoder_1_out15, DR_output_pin_0, DR_output_pin_1,
       DR_output_pin_2, DR_output_pin_3, DR_output_pin_4, DR_output_pin_5, DR_output_pin_6, DR_output_pin_7,
       n16_byte_memory_1_out_28, n16_byte_memory_1_out_29, n16_byte_memory_1_out_30,
       n16_byte_memory_1_out_31, n16_byte_memory_1_out_32, n16_byte_memory_1_out_33,
       n16_byte_memory_1_out_34, n16_byte_memory_1_out_35, not_1_out, or_1_out, or_2_out, or_3_out, or_4_out,
       or_5_out, or_6_out, or_7_out, or_8_out;
  wire [3:0] AR_output_pin_0;

  Falling_4_Bit_Register AR (
    .Input_Pin_0(MAR_0), .Input_Pin_1(MAR_1), .Input_Pin_2(MAR_2), .Input_Pin_3(MAR_3),
    .Output_Pin_0(AR_output_pin_0[0]), .Output_Pin_1(AR_output_pin_0[1]), .Output_Pin_2(AR_output_pin_0[2]),
    .Output_Pin_3(AR_output_pin_0[3]), .Enabler(CU_Enabler), .Clock(Clock), .RESET(RESET));
  Decoder #(.select(4), .enable("false")) decoder_1 (
    .out0(decoder_1_out0), .out1(decoder_1_out1), .out2(decoder_1_out2), .out3(decoder_1_out3),
    .out4(decoder_1_out4), .out5(decoder_1_out5), .out6(decoder_1_out6), .out7(decoder_1_out7),
    .out8(decoder_1_out8), .out9(decoder_1_out9), .out10(decoder_1_out10), .out11(decoder_1_out11),
    .out12(decoder_1_out12), .out13(decoder_1_out13), .out14(decoder_1_out14), .out15(decoder_1_out15),
    .sel(AR_output_pin_0));
  and and_1 (and_1_out, CU_Enabler, R_W, From_MBR_0);
  and and_2 (and_2_out, CU_Enabler, R_W, From_MBR_1);
  and and_3 (and_3_out, CU_Enabler, R_W, From_MBR_2);
  and and_4 (and_4_out, CU_Enabler, R_W, From_MBR_3);
  and and_5 (and_5_out, CU_Enabler, R_W, From_MBR_4);
  and and_6 (and_6_out, CU_Enabler, R_W, From_MBR_5);
  and and_7 (and_7_out, CU_Enabler, R_W, From_MBR_6);
  and and_8 (and_8_out, CU_Enabler, R_W, From_MBR_7);
  not not_1 (not_1_out, R_W);
  _16_Byte_Memory u_16_byte_memory_1 (
    .Clock(Clock), .R_W(R_W), .Decoder_1(decoder_1_out0), .Decoder_2(decoder_1_out1),
    .Decoder_3(decoder_1_out2), .Decoder_5(decoder_1_out4), .Decoder_6(decoder_1_out5),
    .Decoder_7(decoder_1_out6), .Decoder_8(decoder_1_out7), .Decoder_9(decoder_1_out8),
    .Decoder_10(decoder_1_out9), .Decoder_11(decoder_1_out10), .Decoder_12(decoder_1_out11),
    .Decoder_14(decoder_1_out13), .Decoder_15(decoder_1_out14), .Decoder_16(decoder_1_out15),
    .in_20(DR_output_pin_0), .in_21(DR_output_pin_1), .in_22(DR_output_pin_2), .in_23(DR_output_pin_3),
    .in_24(DR_output_pin_4), .in_25(DR_output_pin_5), .in_26(DR_output_pin_6), .in_27(DR_output_pin_7),
    .out_28(n16_byte_memory_1_out_28), .out_29(n16_byte_memory_1_out_29), .out_30(n16_byte_memory_1_out_30),
    .out_31(n16_byte_memory_1_out_31), .out_32(n16_byte_memory_1_out_32), .out_33(n16_byte_memory_1_out_33),
    .out_34(n16_byte_memory_1_out_34), .out_35(n16_byte_memory_1_out_35), .Decoder_4(decoder_1_out3),
    .Decoder_13(decoder_1_out12), .Reset_Pin(RESET));
  or or_1 (or_1_out, and_8_out, n16_byte_memory_1_out_35);
  or or_2 (or_2_out, and_6_out, n16_byte_memory_1_out_33);
  or or_3 (or_3_out, and_7_out, n16_byte_memory_1_out_34);
  and and_9 (To_MBR_7, not_1_out, DR_output_pin_7);
  and and_10 (To_MBR6, not_1_out, DR_output_pin_6);
  or or_4 (or_4_out, and_5_out, n16_byte_memory_1_out_32);
  or or_5 (or_5_out, and_4_out, n16_byte_memory_1_out_31);
  Rising_8_Bit_Register DR (
    .Enabler(CU_Enabler), .Clock(Clock), .Input_Pin_0(or_8_out), .Input_Pin_1(or_6_out),
    .Input_Pin_2(or_7_out), .Input_Pin_3(or_5_out), .Input_Pin_4(or_4_out), .Input_Pin_5(or_2_out),
    .Input_Pin_6(or_3_out), .Input_Pin_7(or_1_out), .Output_Pin_0(DR_output_pin_0),
    .Output_Pin_1(DR_output_pin_1), .Output_Pin_2(DR_output_pin_2), .Output_Pin_3(DR_output_pin_3),
    .Output_Pin_4(DR_output_pin_4), .Output_Pin_5(DR_output_pin_5), .Output_Pin_6(DR_output_pin_6),
    .Output_Pin_7(DR_output_pin_7), .RESET(RESET));
  and and_11 (To_MBR5, not_1_out, DR_output_pin_5);
  and and_12 (To_MBR3, not_1_out, DR_output_pin_3);
  and and_13 (To_MBR4, not_1_out, DR_output_pin_4);
  or or_6 (or_6_out, and_2_out, n16_byte_memory_1_out_29);
  or or_7 (or_7_out, and_3_out, n16_byte_memory_1_out_30);
  or or_8 (or_8_out, and_1_out, n16_byte_memory_1_out_28);
  and and_14 (To_MBR2, not_1_out, DR_output_pin_2);
  and and_15 (To_MBR1, not_1_out, DR_output_pin_1);
  and and_16 (To_MBR0, not_1_out, DR_output_pin_0);

  // Notes on the sheet:
  //   For all input/output pins: 0 is the least significant bit
endmodule

module _16_Byte_Memory (
  input  Clock,
  input  R_W,
  input  Decoder_1,
  input  Reset_Pin,
  input  Decoder_2,
  input  Decoder_3,
  input  Decoder_4,
  input  Decoder_5,
  input  Decoder_6,
  input  Decoder_7,
  input  Decoder_8,
  input  Decoder_9,
  input  Decoder_10,
  input  Decoder_11,
  input  Decoder_12,
  input  Decoder_13,
  input  Decoder_14,
  input  Decoder_15,
  input  Decoder_16,
  input  in_20,
  input  in_21,
  input  in_22,
  input  in_23,
  input  in_24,
  input  in_25,
  input  in_26,
  input  in_27,
  output out_28,
  output out_29,
  output out_30,
  output out_31,
  output out_32,
  output out_33,
  output out_34,
  output out_35
);

  wire n1_byte_storage_1_out_13, n1_byte_storage_1_out_14, n1_byte_storage_1_out_15,
       n1_byte_storage_1_out_16, n1_byte_storage_1_out_17, n1_byte_storage_1_out_18,
       n1_byte_storage_1_out_19, n1_byte_storage_1_to_dr, n1_byte_storage_2_out_13, n1_byte_storage_2_out_14,
       n1_byte_storage_2_out_15, n1_byte_storage_2_out_16, n1_byte_storage_2_out_17,
       n1_byte_storage_2_out_18, n1_byte_storage_2_out_19, n1_byte_storage_2_to_dr, n1_byte_storage_3_out_13,
       n1_byte_storage_3_out_14, n1_byte_storage_3_out_15, n1_byte_storage_3_out_16,
       n1_byte_storage_3_out_17, n1_byte_storage_3_out_18, n1_byte_storage_3_out_19, n1_byte_storage_3_to_dr,
       n1_byte_storage_4_out_13, n1_byte_storage_4_out_14, n1_byte_storage_4_out_15,
       n1_byte_storage_4_out_16, n1_byte_storage_4_out_17, n1_byte_storage_4_out_18,
       n1_byte_storage_4_out_19, n1_byte_storage_4_to_dr, n1_byte_storage_5_out_13, n1_byte_storage_5_out_14,
       n1_byte_storage_5_out_15, n1_byte_storage_5_out_16, n1_byte_storage_5_out_17,
       n1_byte_storage_5_out_18, n1_byte_storage_5_out_19, n1_byte_storage_5_to_dr, n1_byte_storage_6_out_13,
       n1_byte_storage_6_out_14, n1_byte_storage_6_out_15, n1_byte_storage_6_out_16,
       n1_byte_storage_6_out_17, n1_byte_storage_6_out_18, n1_byte_storage_6_out_19, n1_byte_storage_6_to_dr,
       n1_byte_storage_7_out_13, n1_byte_storage_7_out_14, n1_byte_storage_7_out_15,
       n1_byte_storage_7_out_16, n1_byte_storage_7_out_17, n1_byte_storage_7_out_18,
       n1_byte_storage_7_out_19, n1_byte_storage_7_to_dr, n1_byte_storage_8_out_13, n1_byte_storage_8_out_14,
       n1_byte_storage_8_out_15, n1_byte_storage_8_out_16, n1_byte_storage_8_out_17,
       n1_byte_storage_8_out_18, n1_byte_storage_8_out_19, n1_byte_storage_8_to_dr, n1_byte_storage_9_out_13,
       n1_byte_storage_9_out_14, n1_byte_storage_9_out_15, n1_byte_storage_9_out_16,
       n1_byte_storage_9_out_17, n1_byte_storage_9_out_18, n1_byte_storage_9_out_19, n1_byte_storage_9_to_dr,
       n1_byte_storage_10_out_13, n1_byte_storage_10_out_14, n1_byte_storage_10_out_15,
       n1_byte_storage_10_out_16, n1_byte_storage_10_out_17, n1_byte_storage_10_out_18,
       n1_byte_storage_10_out_19, n1_byte_storage_10_to_dr, n1_byte_storage_11_out_13,
       n1_byte_storage_11_out_14, n1_byte_storage_11_out_15, n1_byte_storage_11_out_16,
       n1_byte_storage_11_out_17, n1_byte_storage_11_out_18, n1_byte_storage_11_out_19,
       n1_byte_storage_11_to_dr, n1_byte_storage_12_out_13, n1_byte_storage_12_out_14,
       n1_byte_storage_12_out_15, n1_byte_storage_12_out_16, n1_byte_storage_12_out_17,
       n1_byte_storage_12_out_18, n1_byte_storage_12_out_19, n1_byte_storage_12_to_dr,
       n1_byte_storage_13_out_13, n1_byte_storage_13_out_14, n1_byte_storage_13_out_15,
       n1_byte_storage_13_out_16, n1_byte_storage_13_out_17, n1_byte_storage_13_out_18,
       n1_byte_storage_13_out_19, n1_byte_storage_13_to_dr, n1_byte_storage_14_out_13,
       n1_byte_storage_14_out_14, n1_byte_storage_14_out_15, n1_byte_storage_14_out_16,
       n1_byte_storage_14_out_17, n1_byte_storage_14_out_18, n1_byte_storage_14_out_19,
       n1_byte_storage_14_to_dr, n1_byte_storage_15_out_13, n1_byte_storage_15_out_14,
       n1_byte_storage_15_out_15, n1_byte_storage_15_out_16, n1_byte_storage_15_out_17,
       n1_byte_storage_15_out_18, n1_byte_storage_15_out_19, n1_byte_storage_15_to_dr,
       n1_byte_storage_16_out_13, n1_byte_storage_16_out_14, n1_byte_storage_16_out_15,
       n1_byte_storage_16_out_16, n1_byte_storage_16_out_17, n1_byte_storage_16_out_18,
       n1_byte_storage_16_out_19, n1_byte_storage_16_to_dr;

  _1_Byte_Storage u_1_byte_storage_1 (
    .in_2(Clock), .Decoder(Decoder_1), .R_W(R_W), .in_5(in_20), .in_6(in_21), .in_7(in_22), .in_8(in_23),
    .in_9(in_24), .in_10(in_25), .in_11(in_26), .From_DR(in_27), .Reset_Pin(Reset_Pin),
    .out_13(n1_byte_storage_1_out_13), .out_14(n1_byte_storage_1_out_14), .out_15(n1_byte_storage_1_out_15),
    .out_16(n1_byte_storage_1_out_16), .out_17(n1_byte_storage_1_out_17), .out_18(n1_byte_storage_1_out_18),
    .out_19(n1_byte_storage_1_out_19), .To_DR(n1_byte_storage_1_to_dr));
  _1_Byte_Storage u_1_byte_storage_2 (
    .in_2(Clock), .Decoder(Decoder_2), .R_W(R_W), .in_5(in_20), .in_6(in_21), .in_7(in_22), .in_8(in_23),
    .in_9(in_24), .in_10(in_25), .in_11(in_26), .From_DR(in_27), .Reset_Pin(Reset_Pin),
    .out_13(n1_byte_storage_2_out_13), .out_14(n1_byte_storage_2_out_14), .out_15(n1_byte_storage_2_out_15),
    .out_16(n1_byte_storage_2_out_16), .out_17(n1_byte_storage_2_out_17), .out_18(n1_byte_storage_2_out_18),
    .out_19(n1_byte_storage_2_out_19), .To_DR(n1_byte_storage_2_to_dr));
  _1_Byte_Storage u_1_byte_storage_3 (
    .in_2(Clock), .Decoder(Decoder_3), .R_W(R_W), .in_5(in_20), .in_6(in_21), .in_7(in_22), .in_8(in_23),
    .in_9(in_24), .in_10(in_25), .in_11(in_26), .From_DR(in_27), .Reset_Pin(Reset_Pin),
    .out_13(n1_byte_storage_3_out_13), .out_14(n1_byte_storage_3_out_14), .out_15(n1_byte_storage_3_out_15),
    .out_16(n1_byte_storage_3_out_16), .out_17(n1_byte_storage_3_out_17), .out_18(n1_byte_storage_3_out_18),
    .out_19(n1_byte_storage_3_out_19), .To_DR(n1_byte_storage_3_to_dr));
  _1_Byte_Storage u_1_byte_storage_4 (
    .in_2(Clock), .Decoder(Decoder_4), .R_W(R_W), .in_5(in_20), .in_6(in_21), .in_7(in_22), .in_8(in_23),
    .in_9(in_24), .in_10(in_25), .in_11(in_26), .From_DR(in_27), .Reset_Pin(Reset_Pin),
    .out_13(n1_byte_storage_4_out_13), .out_14(n1_byte_storage_4_out_14), .out_15(n1_byte_storage_4_out_15),
    .out_16(n1_byte_storage_4_out_16), .out_17(n1_byte_storage_4_out_17), .out_18(n1_byte_storage_4_out_18),
    .out_19(n1_byte_storage_4_out_19), .To_DR(n1_byte_storage_4_to_dr));
  _1_Byte_Storage u_1_byte_storage_5 (
    .in_2(Clock), .Decoder(Decoder_5), .R_W(R_W), .in_5(in_20), .in_6(in_21), .in_7(in_22), .in_8(in_23),
    .in_9(in_24), .in_10(in_25), .in_11(in_26), .From_DR(in_27), .Reset_Pin(Reset_Pin),
    .out_13(n1_byte_storage_5_out_13), .out_14(n1_byte_storage_5_out_14), .out_15(n1_byte_storage_5_out_15),
    .out_16(n1_byte_storage_5_out_16), .out_17(n1_byte_storage_5_out_17), .out_18(n1_byte_storage_5_out_18),
    .out_19(n1_byte_storage_5_out_19), .To_DR(n1_byte_storage_5_to_dr));
  _1_Byte_Storage u_1_byte_storage_6 (
    .in_2(Clock), .Decoder(Decoder_6), .R_W(R_W), .in_5(in_20), .in_6(in_21), .in_7(in_22), .in_8(in_23),
    .in_9(in_24), .in_10(in_25), .in_11(in_26), .From_DR(in_27), .Reset_Pin(Reset_Pin),
    .out_13(n1_byte_storage_6_out_13), .out_14(n1_byte_storage_6_out_14), .out_15(n1_byte_storage_6_out_15),
    .out_16(n1_byte_storage_6_out_16), .out_17(n1_byte_storage_6_out_17), .out_18(n1_byte_storage_6_out_18),
    .out_19(n1_byte_storage_6_out_19), .To_DR(n1_byte_storage_6_to_dr));
  _1_Byte_Storage u_1_byte_storage_7 (
    .in_2(Clock), .Decoder(Decoder_7), .R_W(R_W), .in_5(in_20), .in_6(in_21), .in_7(in_22), .in_8(in_23),
    .in_9(in_24), .in_10(in_25), .in_11(in_26), .From_DR(in_27), .Reset_Pin(Reset_Pin),
    .out_13(n1_byte_storage_7_out_13), .out_14(n1_byte_storage_7_out_14), .out_15(n1_byte_storage_7_out_15),
    .out_16(n1_byte_storage_7_out_16), .out_17(n1_byte_storage_7_out_17), .out_18(n1_byte_storage_7_out_18),
    .out_19(n1_byte_storage_7_out_19), .To_DR(n1_byte_storage_7_to_dr));
  _1_Byte_Storage u_1_byte_storage_8 (
    .in_2(Clock), .Decoder(Decoder_8), .R_W(R_W), .in_5(in_20), .in_6(in_21), .in_7(in_22), .in_8(in_23),
    .in_9(in_24), .in_10(in_25), .in_11(in_26), .From_DR(in_27), .Reset_Pin(Reset_Pin),
    .out_13(n1_byte_storage_8_out_13), .out_14(n1_byte_storage_8_out_14), .out_15(n1_byte_storage_8_out_15),
    .out_16(n1_byte_storage_8_out_16), .out_17(n1_byte_storage_8_out_17), .out_18(n1_byte_storage_8_out_18),
    .out_19(n1_byte_storage_8_out_19), .To_DR(n1_byte_storage_8_to_dr));
  _1_Byte_Storage u_1_byte_storage_9 (
    .in_2(Clock), .Decoder(Decoder_9), .R_W(R_W), .in_5(in_20), .in_6(in_21), .in_7(in_22), .in_8(in_23),
    .in_9(in_24), .in_10(in_25), .in_11(in_26), .From_DR(in_27), .Reset_Pin(Reset_Pin),
    .out_13(n1_byte_storage_9_out_13), .out_14(n1_byte_storage_9_out_14), .out_15(n1_byte_storage_9_out_15),
    .out_16(n1_byte_storage_9_out_16), .out_17(n1_byte_storage_9_out_17), .out_18(n1_byte_storage_9_out_18),
    .out_19(n1_byte_storage_9_out_19), .To_DR(n1_byte_storage_9_to_dr));
  _1_Byte_Storage u_1_byte_storage_10 (
    .in_2(Clock), .Decoder(Decoder_10), .R_W(R_W), .in_5(in_20), .in_6(in_21), .in_7(in_22), .in_8(in_23),
    .in_9(in_24), .in_10(in_25), .in_11(in_26), .From_DR(in_27), .Reset_Pin(Reset_Pin),
    .out_13(n1_byte_storage_10_out_13), .out_14(n1_byte_storage_10_out_14),
    .out_15(n1_byte_storage_10_out_15), .out_16(n1_byte_storage_10_out_16),
    .out_17(n1_byte_storage_10_out_17), .out_18(n1_byte_storage_10_out_18),
    .out_19(n1_byte_storage_10_out_19), .To_DR(n1_byte_storage_10_to_dr));
  _1_Byte_Storage u_1_byte_storage_11 (
    .in_2(Clock), .Decoder(Decoder_11), .R_W(R_W), .in_5(in_20), .in_6(in_21), .in_7(in_22), .in_8(in_23),
    .in_9(in_24), .in_10(in_25), .in_11(in_26), .From_DR(in_27), .Reset_Pin(Reset_Pin),
    .out_13(n1_byte_storage_11_out_13), .out_14(n1_byte_storage_11_out_14),
    .out_15(n1_byte_storage_11_out_15), .out_16(n1_byte_storage_11_out_16),
    .out_17(n1_byte_storage_11_out_17), .out_18(n1_byte_storage_11_out_18),
    .out_19(n1_byte_storage_11_out_19), .To_DR(n1_byte_storage_11_to_dr));
  _1_Byte_Storage u_1_byte_storage_12 (
    .in_2(Clock), .Decoder(Decoder_12), .R_W(R_W), .in_5(in_20), .in_6(in_21), .in_7(in_22), .in_8(in_23),
    .in_9(in_24), .in_10(in_25), .in_11(in_26), .From_DR(in_27), .Reset_Pin(Reset_Pin),
    .out_13(n1_byte_storage_12_out_13), .out_14(n1_byte_storage_12_out_14),
    .out_15(n1_byte_storage_12_out_15), .out_16(n1_byte_storage_12_out_16),
    .out_17(n1_byte_storage_12_out_17), .out_18(n1_byte_storage_12_out_18),
    .out_19(n1_byte_storage_12_out_19), .To_DR(n1_byte_storage_12_to_dr));
  _1_Byte_Storage u_1_byte_storage_13 (
    .in_2(Clock), .Decoder(Decoder_13), .R_W(R_W), .in_5(in_20), .in_6(in_21), .in_7(in_22), .in_8(in_23),
    .in_9(in_24), .in_10(in_25), .in_11(in_26), .From_DR(in_27), .Reset_Pin(Reset_Pin),
    .out_13(n1_byte_storage_13_out_13), .out_14(n1_byte_storage_13_out_14),
    .out_15(n1_byte_storage_13_out_15), .out_16(n1_byte_storage_13_out_16),
    .out_17(n1_byte_storage_13_out_17), .out_18(n1_byte_storage_13_out_18),
    .out_19(n1_byte_storage_13_out_19), .To_DR(n1_byte_storage_13_to_dr));
  _1_Byte_Storage u_1_byte_storage_14 (
    .in_2(Clock), .Decoder(Decoder_14), .R_W(R_W), .in_5(in_20), .in_6(in_21), .in_7(in_22), .in_8(in_23),
    .in_9(in_24), .in_10(in_25), .in_11(in_26), .From_DR(in_27), .Reset_Pin(Reset_Pin),
    .out_13(n1_byte_storage_14_out_13), .out_14(n1_byte_storage_14_out_14),
    .out_15(n1_byte_storage_14_out_15), .out_16(n1_byte_storage_14_out_16),
    .out_17(n1_byte_storage_14_out_17), .out_18(n1_byte_storage_14_out_18),
    .out_19(n1_byte_storage_14_out_19), .To_DR(n1_byte_storage_14_to_dr));
  _1_Byte_Storage u_1_byte_storage_15 (
    .in_2(Clock), .Decoder(Decoder_15), .R_W(R_W), .in_5(in_20), .in_6(in_21), .in_7(in_22), .in_8(in_23),
    .in_9(in_24), .in_10(in_25), .in_11(in_26), .From_DR(in_27), .Reset_Pin(Reset_Pin),
    .out_13(n1_byte_storage_15_out_13), .out_14(n1_byte_storage_15_out_14),
    .out_15(n1_byte_storage_15_out_15), .out_16(n1_byte_storage_15_out_16),
    .out_17(n1_byte_storage_15_out_17), .out_18(n1_byte_storage_15_out_18),
    .out_19(n1_byte_storage_15_out_19), .To_DR(n1_byte_storage_15_to_dr));
  _1_Byte_Storage u_1_byte_storage_16 (
    .in_2(Clock), .Decoder(Decoder_16), .R_W(R_W), .in_5(in_20), .in_6(in_21), .in_7(in_22), .in_8(in_23),
    .in_9(in_24), .in_10(in_25), .in_11(in_26), .From_DR(in_27), .Reset_Pin(Reset_Pin),
    .out_13(n1_byte_storage_16_out_13), .out_14(n1_byte_storage_16_out_14),
    .out_15(n1_byte_storage_16_out_15), .out_16(n1_byte_storage_16_out_16),
    .out_17(n1_byte_storage_16_out_17), .out_18(n1_byte_storage_16_out_18),
    .out_19(n1_byte_storage_16_out_19), .To_DR(n1_byte_storage_16_to_dr));
  _16_Bit_Data_Merger u_16_bit_data_merger_1 (
    .in_1(n1_byte_storage_1_out_13), .in_2(n1_byte_storage_2_out_13), .in_3(n1_byte_storage_3_out_13),
    .in_4(n1_byte_storage_4_out_13), .in_5(n1_byte_storage_5_out_13), .in_6(n1_byte_storage_6_out_13),
    .in_7(n1_byte_storage_7_out_13), .in_8(n1_byte_storage_8_out_13), .in_9(n1_byte_storage_9_out_13),
    .in_10(n1_byte_storage_11_out_13), .in_11(n1_byte_storage_12_out_13), .in_12(n1_byte_storage_13_out_13),
    .in_13(n1_byte_storage_14_out_13), .in_14(n1_byte_storage_15_out_13), .in_15(n1_byte_storage_16_out_13),
    .in_16(n1_byte_storage_10_out_13), .out_17(out_28));
  _16_Bit_Data_Merger u_16_bit_data_merger_2 (
    .in_1(n1_byte_storage_1_out_14), .in_2(n1_byte_storage_2_out_14), .in_3(n1_byte_storage_3_out_14),
    .in_4(n1_byte_storage_4_out_14), .in_5(n1_byte_storage_5_out_14), .in_6(n1_byte_storage_6_out_14),
    .in_7(n1_byte_storage_7_out_14), .in_8(n1_byte_storage_8_out_14), .in_9(n1_byte_storage_9_out_14),
    .in_10(n1_byte_storage_10_out_14), .in_11(n1_byte_storage_11_out_14), .in_12(n1_byte_storage_12_out_14),
    .in_13(n1_byte_storage_13_out_14), .in_14(n1_byte_storage_14_out_14), .in_15(n1_byte_storage_15_out_14),
    .in_16(n1_byte_storage_16_out_14), .out_17(out_29));
  _16_Bit_Data_Merger u_16_bit_data_merger_3 (
    .in_1(n1_byte_storage_16_out_15), .in_2(n1_byte_storage_1_out_15), .in_3(n1_byte_storage_2_out_15),
    .in_4(n1_byte_storage_3_out_15), .in_5(n1_byte_storage_4_out_15), .in_6(n1_byte_storage_5_out_15),
    .in_7(n1_byte_storage_6_out_15), .in_8(n1_byte_storage_7_out_15), .in_9(n1_byte_storage_8_out_15),
    .in_10(n1_byte_storage_9_out_15), .in_11(n1_byte_storage_10_out_15), .in_12(n1_byte_storage_11_out_15),
    .in_13(n1_byte_storage_12_out_15), .in_14(n1_byte_storage_13_out_15), .in_15(n1_byte_storage_14_out_15),
    .in_16(n1_byte_storage_15_out_15), .out_17(out_30));
  _16_Bit_Data_Merger u_16_bit_data_merger_4 (
    .in_1(n1_byte_storage_1_out_16), .in_2(n1_byte_storage_2_out_16), .in_3(n1_byte_storage_3_out_16),
    .in_4(n1_byte_storage_5_out_16), .in_5(n1_byte_storage_6_out_16), .in_6(n1_byte_storage_8_out_16),
    .in_7(n1_byte_storage_9_out_16), .in_8(n1_byte_storage_10_out_16), .in_9(n1_byte_storage_11_out_16),
    .in_10(n1_byte_storage_12_out_16), .in_11(n1_byte_storage_13_out_16), .in_12(n1_byte_storage_14_out_16),
    .in_13(n1_byte_storage_15_out_16), .in_14(n1_byte_storage_16_out_16), .in_15(n1_byte_storage_7_out_16),
    .in_16(n1_byte_storage_4_out_16), .out_17(out_31));
  _16_Bit_Data_Merger u_16_bit_data_merger_5 (
    .in_1(n1_byte_storage_1_out_17), .in_2(n1_byte_storage_2_out_17), .in_3(n1_byte_storage_3_out_17),
    .in_4(n1_byte_storage_4_out_17), .in_5(n1_byte_storage_5_out_17), .in_6(n1_byte_storage_6_out_17),
    .in_7(n1_byte_storage_7_out_17), .in_8(n1_byte_storage_8_out_17), .in_9(n1_byte_storage_9_out_17),
    .in_10(n1_byte_storage_10_out_17), .in_11(n1_byte_storage_11_out_17), .in_12(n1_byte_storage_12_out_17),
    .in_13(n1_byte_storage_13_out_17), .in_14(n1_byte_storage_14_out_17), .in_15(n1_byte_storage_15_out_17),
    .in_16(n1_byte_storage_16_out_17), .out_17(out_32));
  _16_Bit_Data_Merger u_16_bit_data_merger_6 (
    .in_1(n1_byte_storage_1_out_18), .in_2(n1_byte_storage_2_out_18), .in_3(n1_byte_storage_3_out_18),
    .in_4(n1_byte_storage_4_out_18), .in_5(n1_byte_storage_5_out_18), .in_6(n1_byte_storage_6_out_18),
    .in_7(n1_byte_storage_7_out_18), .in_8(n1_byte_storage_8_out_18), .in_9(n1_byte_storage_9_out_18),
    .in_10(n1_byte_storage_10_out_18), .in_11(n1_byte_storage_11_out_18), .in_12(n1_byte_storage_12_out_18),
    .in_13(n1_byte_storage_13_out_18), .in_14(n1_byte_storage_14_out_18), .in_15(n1_byte_storage_15_out_18),
    .in_16(n1_byte_storage_16_out_18), .out_17(out_33));
  _16_Bit_Data_Merger u_16_bit_data_merger_7 (
    .in_1(n1_byte_storage_1_out_19), .in_2(n1_byte_storage_2_out_19), .in_3(n1_byte_storage_3_out_19),
    .in_4(n1_byte_storage_4_out_19), .in_5(n1_byte_storage_5_out_19), .in_6(n1_byte_storage_6_out_19),
    .in_7(n1_byte_storage_7_out_19), .in_8(n1_byte_storage_8_out_19), .in_9(n1_byte_storage_9_out_19),
    .in_10(n1_byte_storage_10_out_19), .in_11(n1_byte_storage_11_out_19), .in_12(n1_byte_storage_12_out_19),
    .in_13(n1_byte_storage_13_out_19), .in_14(n1_byte_storage_14_out_19), .in_15(n1_byte_storage_15_out_19),
    .in_16(n1_byte_storage_16_out_19), .out_17(out_34));
  _16_Bit_Data_Merger u_16_bit_data_merger_8 (
    .in_1(n1_byte_storage_1_to_dr), .in_2(n1_byte_storage_2_to_dr), .in_3(n1_byte_storage_3_to_dr),
    .in_4(n1_byte_storage_4_to_dr), .in_5(n1_byte_storage_5_to_dr), .in_6(n1_byte_storage_6_to_dr),
    .in_7(n1_byte_storage_12_to_dr), .in_8(n1_byte_storage_13_to_dr), .in_9(n1_byte_storage_14_to_dr),
    .in_10(n1_byte_storage_15_to_dr), .in_11(n1_byte_storage_16_to_dr), .in_12(n1_byte_storage_11_to_dr),
    .in_13(n1_byte_storage_7_to_dr), .in_14(n1_byte_storage_10_to_dr), .in_15(n1_byte_storage_9_to_dr),
    .in_16(n1_byte_storage_8_to_dr), .out_17(out_35));
endmodule

module _1_Byte_Storage (
  input  Reset_Pin,
  input  in_2,
  input  Decoder,
  input  R_W,
  input  in_5,
  input  in_6,
  input  in_7,
  input  in_8,
  input  in_9,
  input  in_10,
  input  in_11,
  input  From_DR,
  output out_13,
  output out_14,
  output out_15,
  output out_16,
  output out_17,
  output out_18,
  output out_19,
  output To_DR
);

  wire and_1_out, and_2_out, and_3_out, and_4_out, and_5_out, and_6_out, and_7_out, and_8_out, and_9_out,
       n8_bit_register_1_out_12, n8_bit_register_1_out_13, n8_bit_register_1_out_14,
       n8_bit_register_1_out_15, n8_bit_register_1_out_16, n8_bit_register_1_out_18,
       n8_bit_register_1_out_19, n8_bit_register_1_output_pins, not_1_out;

  and and_1 (and_1_out, Decoder, in_5, R_W);
  and and_2 (and_2_out, Decoder, in_6, R_W);
  and and_3 (and_3_out, Decoder, in_7, R_W);
  and and_4 (and_4_out, Decoder, in_8, R_W);
  and and_5 (and_5_out, Decoder, in_9, R_W);
  and and_6 (and_6_out, Decoder, in_10, R_W);
  and and_7 (and_7_out, Decoder, in_11, R_W);
  and and_8 (and_8_out, Decoder, From_DR, R_W);
  and and_9 (and_9_out, Decoder, R_W);
  _8_Bit_Register u_8_bit_register_1 (
    .clock(in_2), .Enabler(and_9_out), .in_4(and_1_out), .in_5(and_2_out), .in_6(and_3_out),
    .in_7(and_4_out), .in_8(and_5_out), .in_9(and_6_out), .input_pins(and_7_out), .in_11(and_8_out),
    .out_12(n8_bit_register_1_out_12), .out_13(n8_bit_register_1_out_13), .out_14(n8_bit_register_1_out_14),
    .out_15(n8_bit_register_1_out_15), .out_16(n8_bit_register_1_out_16),
    .output_pins(n8_bit_register_1_output_pins), .out_18(n8_bit_register_1_out_18),
    .out_19(n8_bit_register_1_out_19), .in_2(Reset_Pin));
  not not_1 (not_1_out, R_W);
  and and_10 (out_13, not_1_out, n8_bit_register_1_out_12, Decoder);
  and and_11 (out_14, not_1_out, n8_bit_register_1_out_13, Decoder);
  and and_12 (out_15, not_1_out, n8_bit_register_1_out_14, Decoder);
  and and_13 (out_16, not_1_out, n8_bit_register_1_out_15, Decoder);
  and and_14 (out_17, not_1_out, n8_bit_register_1_out_16, Decoder);
  and and_15 (out_18, not_1_out, n8_bit_register_1_output_pins, Decoder);
  and and_16 (out_19, not_1_out, n8_bit_register_1_out_18, Decoder);
  and and_17 (To_DR, not_1_out, n8_bit_register_1_out_19, Decoder);
endmodule

module _8_Bit_Register (
  input  clock,
  input  in_2,
  input  Enabler,
  input  in_4,
  input  in_5,
  input  in_6,
  input  in_7,
  input  in_8,
  input  in_9,
  input  input_pins,
  input  in_11,
  output out_12,
  output out_13,
  output out_14,
  output out_15,
  output out_16,
  output output_pins,
  output out_18,
  output out_19
);

  D_Flip_Flop d_ff_1 (.clk(clock), .D(in_4), .Q(out_12), .en(Enabler), .reset(in_2));  // open: Qn, preset
  D_Flip_Flop d_ff_2 (.clk(clock), .D(in_5), .Q(out_13), .en(Enabler), .reset(in_2));  // open: Qn, preset
  D_Flip_Flop d_ff_3 (.clk(clock), .D(in_6), .Q(out_14), .en(Enabler), .reset(in_2));  // open: Qn, preset
  D_Flip_Flop d_ff_4 (.clk(clock), .D(in_7), .Q(out_15), .en(Enabler), .reset(in_2));  // open: Qn, preset
  D_Flip_Flop d_ff_5 (.clk(clock), .D(in_8), .Q(out_16), .en(Enabler), .reset(in_2));  // open: Qn, preset
  D_Flip_Flop d_ff_6 (.clk(clock), .D(in_9), .Q(output_pins), .en(Enabler), .reset(in_2));  // open: Qn, preset
  D_Flip_Flop d_ff_7 (.clk(clock), .D(input_pins), .Q(out_18), .en(Enabler), .reset(in_2));  // open: Qn, preset
  D_Flip_Flop d_ff_8 (.clk(clock), .D(in_11), .Q(out_19), .en(Enabler), .reset(in_2));  // open: Qn, preset

  // Notes on the sheet:
  //   enabler
endmodule

module _16_Bit_Data_Merger (
  input  in_1,
  input  in_2,
  input  in_3,
  input  in_4,
  input  in_5,
  input  in_6,
  input  in_7,
  input  in_8,
  input  in_9,
  input  in_10,
  input  in_11,
  input  in_12,
  input  in_13,
  input  in_14,
  input  in_15,
  input  in_16,
  output out_17
);

  wire or_1_out, or_2_out, or_3_out;

  or or_1 (or_1_out, in_1, in_2, in_3, in_4, in_5);
  or or_2 (or_2_out, or_1_out, in_6, in_7, in_8, in_9);
  or or_3 (or_3_out, or_2_out, in_10, in_11, in_12, in_13);
  or or_4 (out_17, or_3_out, in_14, in_15, in_16);
endmodule
