// Logisim project ROM.circ as structural Verilog: 3 circuits, main circuit ROM Data
module ROM (
  input  Clock,
  input  Enabler,
  output [3:0] Address,
  output [7:0] Data,
  output ROMend
);

  wire and_1_out, d_ff_1_q, d_ff_2_q, d_ff_3_q, rom_addresses_1_carry;

  and and_1 (and_1_out, Enabler, ~d_ff_2_q);  // AND_Gate
  ROM_Data rom_data_1 (.Enabler(and_1_out), .Clock(Clock), .Data_Output(Data));
  ROM_Addresses rom_addresses_1 (
    .Enabler(and_1_out), .Clock(Clock), .Address_Output(Address), .carry(rom_addresses_1_carry));
  D_Flip_Flop d_ff_1 (.clk(Clock), .D(rom_addresses_1_carry), .Q(d_ff_1_q));  // open: Qn, preset, en, reset
  D_Flip_Flop d_ff_2 (.clk(Clock), .D(d_ff_1_q), .Q(d_ff_2_q));  // open: Qn, preset, en, reset
  D_Flip_Flop d_ff_3 (.clk(Clock), .D(d_ff_2_q), .Q(d_ff_3_q));  // open: Qn, preset, en, reset
  D_Flip_Flop d_ff_4 (.clk(Clock), .D(d_ff_3_q), .Q(ROMend));  // open: Qn, preset, en, reset
endmodule

module ROM_Data (
  input  Enabler,
  input  Clock,
  output [7:0] Data_Output
);

  wire and_1_out, d_ff_1_q, rising_4_bit_register_1_output_pin_0, rising_4_bit_register_1_output_pin_1,
       rising_4_bit_register_1_output_pin_2, rising_4_bit_register_1_output_pin_3;
  wire [3:0] adder_1_out, multiplexer_2_out, rising_4_bit_register_2_output_pin_0;

  Rising_4_Bit_Register rising_4_bit_register_1 (
    .Input_Pin_0(adder_1_out[0]), .Input_Pin_1(adder_1_out[1]), .Input_Pin_2(adder_1_out[2]),
    .Input_Pin_3(adder_1_out[3]), .Output_Pin_0(rising_4_bit_register_1_output_pin_0),
    .Output_Pin_1(rising_4_bit_register_1_output_pin_1), .Output_Pin_2(rising_4_bit_register_1_output_pin_2),
    .Output_Pin_3(rising_4_bit_register_1_output_pin_3), .Enabler(Enabler), .Clock(Clock));  // open: RESET
  Rising_4_Bit_Register rising_4_bit_register_2 (
    .Input_Pin_0(rising_4_bit_register_1_output_pin_0), .Input_Pin_1(rising_4_bit_register_1_output_pin_1),
    .Input_Pin_2(rising_4_bit_register_1_output_pin_2), .Input_Pin_3(rising_4_bit_register_1_output_pin_3),
    .Output_Pin_0(rising_4_bit_register_2_output_pin_0[0]),
    .Output_Pin_1(rising_4_bit_register_2_output_pin_0[1]),
    .Output_Pin_2(rising_4_bit_register_2_output_pin_0[2]),
    .Output_Pin_3(rising_4_bit_register_2_output_pin_0[3]), .Enabler(Enabler), .Clock(Clock));  // open: RESET
  Multiplexer #(.select(4), .width(8), .enable("false")) multiplexer_1 (
    .in0(8'h8f), .in1(8'hc), .in2(8'he0), .in3({8{1'b1}}), .in4(8'h2b), .in5(8'hc0), .in6(8'h9e),
    .in7({8{1'b0}}), .in8(8'hae), .in9(8'h92), .in10(8'h40), .in11(8'h8e), .in12(8'he0), .in13({8{1'b1}}),
    .in14({8{1'b0}}), .in15(8'h5), .out(Data_Output), .sel(multiplexer_2_out));
  Multiplexer #(.width(4), .enable("false")) multiplexer_2 (
    .in0(rising_4_bit_register_2_output_pin_0), .in1(4'b1111), .out(multiplexer_2_out), .sel(d_ff_1_q));
  D_Flip_Flop d_ff_1 (.Q(d_ff_1_q), .preset(and_1_out));  // open: clk, D, Qn, en, reset
  and and_1 (and_1_out, rising_4_bit_register_1_output_pin_2, rising_4_bit_register_2_output_pin_0[3], rising_4_bit_register_1_output_pin_0, rising_4_bit_register_1_output_pin_1, rising_4_bit_register_1_output_pin_3, rising_4_bit_register_2_output_pin_0[0], rising_4_bit_register_2_output_pin_0[1], rising_4_bit_register_2_output_pin_0[2]);
  Adder #(.width(4)) adder_1 (
    .a(rising_4_bit_register_2_output_pin_0), .b(4'b0001), .out(adder_1_out));  // open: cin, cout

  // Notes on the sheet:
  //   Number 2
endmodule

module ROM_Addresses (
  input  Clock,
  input  Enabler,
  output [3:0] Address_Output,
  output carry
);

  wire falling_4_bit_register_1_output_pin_0, falling_4_bit_register_1_output_pin_1,
       falling_4_bit_register_1_output_pin_2, falling_4_bit_register_1_output_pin_3;
  wire [3:0] adder_1_out, falling_4_bit_register_2_output_pin_0;

  Falling_4_Bit_Register falling_4_bit_register_1 (
    .Input_Pin_0(adder_1_out[0]), .Input_Pin_1(adder_1_out[1]), .Input_Pin_2(adder_1_out[2]),
    .Input_Pin_3(adder_1_out[3]), .Output_Pin_0(falling_4_bit_register_1_output_pin_0),
    .Output_Pin_1(falling_4_bit_register_1_output_pin_1),
    .Output_Pin_2(falling_4_bit_register_1_output_pin_2),
    .Output_Pin_3(falling_4_bit_register_1_output_pin_3), .Enabler(Enabler), .Clock(Clock));  // open: RESET
  Multiplexer #(.select(4), .width(4), .enable("false")) multiplexer_1 (
    .in0(4'b0000), .in1(4'b0001), .in2(4'b0010), .in3(4'b0011), .in4(4'b0100), .in5(4'b0101), .in6(4'b0110),
    .in7(4'b0111), .in8(4'b1000), .in9(4'b1001), .in10(4'b1010), .in11(4'b1011), .in12(4'b1100),
    .in13(4'b1101), .in14(4'b1110), .in15(4'b1111), .out(Address_Output),
    .sel(falling_4_bit_register_2_output_pin_0));
  Falling_4_Bit_Register falling_4_bit_register_2 (
    .Input_Pin_0(falling_4_bit_register_1_output_pin_0), .Input_Pin_1(falling_4_bit_register_1_output_pin_1),
    .Input_Pin_2(falling_4_bit_register_1_output_pin_2), .Input_Pin_3(falling_4_bit_register_1_output_pin_3),
    .Output_Pin_0(falling_4_bit_register_2_output_pin_0[0]),
    .Output_Pin_1(falling_4_bit_register_2_output_pin_0[1]),
    .Output_Pin_2(falling_4_bit_register_2_output_pin_0[2]),
    .Output_Pin_3(falling_4_bit_register_2_output_pin_0[3]), .Enabler(Enabler), .Clock(Clock));  // open: RESET
  Adder #(.width(4)) adder_1 (
    .a(falling_4_bit_register_2_output_pin_0), .b(4'b0001), .out(adder_1_out), .cout(carry));  // open: cin
endmodule
