// Logisim project Registers.circ as structural Verilog: 4 circuits, main circuit Rising 8-Bit Register
module Rising_8_Bit_Register (
  input  Enabler,
  input  Clock,
  input  RESET,
  input  Input_Pin_0,
  input  Input_Pin_1,
  input  Input_Pin_2,
  input  Input_Pin_3,
  input  Input_Pin_4,
  input  Input_Pin_5,
  input  Input_Pin_6,
  input  Input_Pin_7,
  output Output_Pin_0,
  output Output_Pin_1,
  output Output_Pin_2,
  output Output_Pin_3,
  output Output_Pin_4,
  output Output_Pin_5,
  output Output_Pin_6,
  output Output_Pin_7
);

  D_Flip_Flop Bit_0 (.clk(Clock), .D(Input_Pin_0), .Q(Output_Pin_0), .en(Enabler), .reset(RESET));  // open: Qn, preset
  D_Flip_Flop Bit_1 (.clk(Clock), .D(Input_Pin_1), .Q(Output_Pin_1), .en(Enabler), .reset(RESET));  // open: Qn, preset
  D_Flip_Flop Bit_2 (.clk(Clock), .D(Input_Pin_2), .Q(Output_Pin_2), .en(Enabler), .reset(RESET));  // open: Qn, preset
  D_Flip_Flop Bit_3 (.clk(Clock), .D(Input_Pin_3), .Q(Output_Pin_3), .en(Enabler), .reset(RESET));  // open: Qn, preset
  D_Flip_Flop Bit_4 (.clk(Clock), .D(Input_Pin_4), .Q(Output_Pin_4), .en(Enabler), .reset(RESET));  // open: Qn, preset
  D_Flip_Flop Bit_5 (.clk(Clock), .D(Input_Pin_5), .Q(Output_Pin_5), .en(Enabler), .reset(RESET));  // open: Qn, preset
  D_Flip_Flop Bit_6 (.clk(Clock), .D(Input_Pin_6), .Q(Output_Pin_6), .en(Enabler), .reset(RESET));  // open: Qn, preset
  D_Flip_Flop Bit_7 (.clk(Clock), .D(Input_Pin_7), .Q(Output_Pin_7), .en(Enabler), .reset(RESET));  // open: Qn, preset
endmodule

module Rising_4_Bit_Register (
  input  Enabler,
  input  Clock,
  input  RESET,
  input  Input_Pin_0,
  input  Input_Pin_1,
  input  Input_Pin_2,
  input  Input_Pin_3,
  output Output_Pin_0,
  output Output_Pin_1,
  output Output_Pin_2,
  output Output_Pin_3
);

  D_Flip_Flop Bit_0 (.clk(Clock), .D(Input_Pin_0), .Q(Output_Pin_0), .en(Enabler), .reset(RESET));  // open: Qn, preset
  D_Flip_Flop Bit_1 (.clk(Clock), .D(Input_Pin_1), .Q(Output_Pin_1), .en(Enabler), .reset(RESET));  // open: Qn, preset
  D_Flip_Flop Bit_2 (.clk(Clock), .D(Input_Pin_2), .Q(Output_Pin_2), .en(Enabler), .reset(RESET));  // open: Qn, preset
  D_Flip_Flop Bit_3 (.clk(Clock), .D(Input_Pin_3), .Q(Output_Pin_3), .en(Enabler), .reset(RESET));  // open: Qn, preset
endmodule

module Falling_8_bit_Register (
  input  Enabler,
  input  Clock,
  input  RESET,
  input  Input_Pin_0,
  input  Input_Pin_1,
  input  Input_Pin_2,
  input  Input_Pin_3,
  input  Input_Pin_4,
  input  Input_Pin_5,
  input  Input_Pin_6,
  input  Input_Pin_7,
  output Output_Pin_0,
  output Output_Pin_1,
  output Output_Pin_2,
  output Output_Pin_3,
  output Output_Pin_4,
  output Output_Pin_5,
  output Output_Pin_6,
  output Output_Pin_7
);

  D_Flip_Flop #(.trigger("falling")) Bit_0 (
    .clk(Clock), .D(Input_Pin_0), .Q(Output_Pin_0), .en(Enabler), .reset(RESET));  // open: Qn, preset
  D_Flip_Flop #(.trigger("falling")) Bit_1 (
    .clk(Clock), .D(Input_Pin_1), .Q(Output_Pin_1), .en(Enabler), .reset(RESET));  // open: Qn, preset
  D_Flip_Flop #(.trigger("falling")) Bit_2 (
    .clk(Clock), .D(Input_Pin_2), .Q(Output_Pin_2), .en(Enabler), .reset(RESET));  // open: Qn, preset
  D_Flip_Flop #(.trigger("falling")) Bit_3 (
    .clk(Clock), .D(Input_Pin_3), .Q(Output_Pin_3), .en(Enabler), .reset(RESET));  // open: Qn, preset
  D_Flip_Flop #(.trigger("falling")) Bit_4 (
    .clk(Clock), .D(Input_Pin_4), .Q(Output_Pin_4), .en(Enabler), .reset(RESET));  // open: Qn, preset
  D_Flip_Flop #(.trigger("falling")) Bit_5 (
    .clk(Clock), .D(Input_Pin_5), .Q(Output_Pin_5), .en(Enabler), .reset(RESET));  // open: Qn, preset
  D_Flip_Flop #(.trigger("falling")) Bit_6 (
    .clk(Clock), .D(Input_Pin_6), .Q(Output_Pin_6), .en(Enabler), .reset(RESET));  // open: Qn, preset
  D_Flip_Flop #(.trigger("falling")) Bit_7 (
    .clk(Clock), .D(Input_Pin_7), .Q(Output_Pin_7), .en(Enabler), .reset(RESET));  // open: Qn, preset
endmodule

module Falling_4_Bit_Register (
  input  Enabler,
  input  Clock,
  input  RESET,
  input  Input_Pin_0,
  input  Input_Pin_1,
  input  Input_Pin_2,
  input  Input_Pin_3,
  output Output_Pin_0,
  output Output_Pin_1,
  output Output_Pin_2,
  output Output_Pin_3
);

  D_Flip_Flop #(.trigger("falling")) Bit_0 (
    .clk(Clock), .D(Input_Pin_0), .Q(Output_Pin_0), .en(Enabler), .reset(RESET));  // open: Qn, preset
  D_Flip_Flop #(.trigger("falling")) Bit_1 (
    .clk(Clock), .D(Input_Pin_1), .Q(Output_Pin_1), .en(Enabler), .reset(RESET));  // open: Qn, preset
  D_Flip_Flop #(.trigger("falling")) Bit_2 (
    .clk(Clock), .D(Input_Pin_2), .Q(Output_Pin_2), .en(Enabler), .reset(RESET));  // open: Qn, preset
  D_Flip_Flop #(.trigger("falling")) Bit_3 (
    .clk(Clock), .D(Input_Pin_3), .Q(Output_Pin_3), .en(Enabler), .reset(RESET));  // open: Qn, preset
endmodule
